// Digital circuit 16 Bit Or Combinator.dig as structural Verilog
module _16_Bit_Or_Combinator (
  input  [15:0] I,
  output O
);

  or or_1 (O, I[0], I[1], I[2], I[3], I[4], I[5], I[6], I[7], I[8], I[9], I[10], I[11], I[12], I[13], I[14], I[15]);
endmodule
