// Digital circuit ALU.dig as structural Verilog
module ALU (
  input  [15:0] DATA_IN_1,
  input  [15:0] DATA_IN_2,
  input  [7:0] F_SEL,
  input  [3:0] SHFT_IN,
  input  F_SET_CLK,
  output [15:0] OUT
);

  wire and_1_out, and_2_out, comparator_1_eq, comparator_1_gt, or_1_out;
  wire [7:0] d_ff_1_q;
  wire [15:0] add_1_s, and_3_out, barrelshifter_1_out, barrelshifter_2_out, driver_8_out, not_1_out, or_2_out;
  wire [31:0] mul_1_mul;

  D_FF #(.Bits(8)) d_ff_1 (.D(F_SEL), .C(F_SET_CLK), .Q(d_ff_1_q));  // open: nQ
  and and_1 (and_1_out, d_ff_1_q[6], comparator_1_gt);
  and and_2 (and_2_out, d_ff_1_q[7], comparator_1_eq);
  assign OUT = or_1_out ? {16{1'b1}} : 16'bz;  // Driver driver_1
  PullDown #(.Bits(16)) pulldown_1 (.out(OUT));
  Comparator #(.Signed("true"), .Bits(16)) comparator_1 (
    .a(DATA_IN_1), .b(DATA_IN_2), .gt(comparator_1_gt), .eq(comparator_1_eq));  // open: lt
  or or_1 (or_1_out, and_1_out, and_2_out);
  Mul #(.Bits(16)) mul_1 (.a(DATA_IN_2), .b(DATA_IN_1), .mul(mul_1_mul));
  assign OUT = d_ff_1_q[5] ? mul_1_mul[15:0] : 16'bz;  // Driver driver_2
  assign OUT = d_ff_1_q[4] ? driver_8_out : 16'bz;  // Driver driver_3
  assign OUT = d_ff_1_q[3] ? add_1_s : 16'bz;  // Driver driver_4
  Add #(.Bits(16)) add_1 (.a(DATA_IN_2), .b(DATA_IN_1), .c_i(1'b0), .s(add_1_s));  // open: c_o
  assign not_1_out = ~DATA_IN_1;  // Not not_1, 16 bits wide
  assign OUT = d_ff_1_q[2] ? not_1_out : 16'bz;  // Driver driver_5
  assign or_2_out = DATA_IN_2 | DATA_IN_1;  // Or or_2, 16 bits wide
  assign OUT = d_ff_1_q[1] ? or_2_out : 16'bz;  // Driver driver_6
  assign and_3_out = DATA_IN_2 & DATA_IN_1;  // And and_3, 16 bits wide
  assign OUT = d_ff_1_q[0] ? and_3_out : 16'bz;  // Driver driver_7
  BarrelShifter #(.Bits(16)) barrelshifter_1 (.in(DATA_IN_1), .shift({2'b00, SHFT_IN[2:0]}), .out(barrelshifter_1_out));
  assign driver_8_out = SHFT_IN[3] ? barrelshifter_1_out : 16'bz;  // Driver driver_8
  BarrelShifter #(.Bits(16), .direction("right")) barrelshifter_2 (
    .in(DATA_IN_1), .shift({2'b00, SHFT_IN[2:0]}), .out(barrelshifter_2_out));
  assign driver_8_out = ~SHFT_IN[3] ? barrelshifter_2_out : 16'bz;  // DriverInvSel driverinvsel_1

  // Notes on the sheet:
  //   F_SEL: One hot!
endmodule
