// Digital circuit ASCIIdisp.dig as structural Verilog
module ASCIIdisp (
  input  [15:0] TEST_DATA,
  input  TEST_SEND,
  input  clk
);

  wire and_1_out, and_2_out, bus_debugger_1_fb, d_ff_2_q, d_ff_3_q, reset_on_first_clock_1_rst;
  wire [2:0] bus_debugger_1_last_addr_out, d_ff_1_q, driver_1_out_2;
  wire [15:0] bus_debugger_1_last_data_out, driver_1_out, keyboard_1_d;

  Reset_On_First_Clock reset_on_first_clock_1 (.CLK(clk), .RST(reset_on_first_clock_1_rst));
  and and_1 (and_1_out, ~driver_1_out[0], bus_debugger_1_fb, clk);  // And
  // Probe CLK on clk
  D_FF #(.Bits(3)) d_ff_1 (.D(driver_1_out_2), .C(and_2_out), .Q(d_ff_1_q));  // open: nQ
  Terminal #(.termWidth(80)) terminal_1 (.D(driver_1_out[15:8]), .C(and_1_out));  // open: en
  Bus_Debugger bus_debugger_1 (
    .DATA({driver_1_out[15:4], driver_1_out_2, driver_1_out[0]}), .ADDR(d_ff_1_q), .TB(d_ff_3_q),
    .TEST_DATA(TEST_DATA), .TEST_SEND(TEST_SEND), .CLK(clk), .FB(bus_debugger_1_fb),
    .LAST_DATA_OUT(bus_debugger_1_last_data_out), .LAST_ADDR_OUT(bus_debugger_1_last_addr_out));
  and and_2 (and_2_out, ~reset_on_first_clock_1_rst, driver_1_out[0]);  // And
  D_FF d_ff_2 (.D(and_2_out), .C(clk), .Q(d_ff_2_q));  // open: nQ
  assign {driver_1_out[15:4], driver_1_out_2, driver_1_out[0]} = d_ff_3_q ? keyboard_1_d : 16'bz;  // Driver driver_1
  D_FF d_ff_3 (.D(d_ff_2_q), .C(~clk), .Q(d_ff_3_q));  // open: nQ
  Keyboard keyboard_1 (.C(d_ff_2_q), .D(keyboard_1_d));  // open: en, av
  LED led_1 (.in(bus_debugger_1_last_data_out[1]));
  LED led_2 (.in(bus_debugger_1_last_data_out[0]));
  LED led_3 (.in(bus_debugger_1_last_data_out[3]));
  LED led_4 (.in(bus_debugger_1_last_data_out[5]));
  LED led_5 (.in(bus_debugger_1_last_data_out[2]));
  LED led_6 (.in(bus_debugger_1_last_data_out[4]));
  LED led_7 (.in(bus_debugger_1_last_data_out[7]));
  LED led_8 (.in(bus_debugger_1_last_data_out[9]));
  LED led_9 (.in(bus_debugger_1_last_data_out[6]));
  LED led_10 (.in(bus_debugger_1_last_data_out[8]));
  LED led_11 (.in(bus_debugger_1_last_data_out[11]));
  LED led_12 (.in(bus_debugger_1_last_data_out[13]));
  LED led_13 (.in(bus_debugger_1_last_data_out[10]));
  LED led_14 (.in(bus_debugger_1_last_data_out[12]));
  LED led_15 (.in(bus_debugger_1_last_data_out[15]));
  LED led_16 (.in(bus_debugger_1_last_data_out[14]));
  LED led_17 (.in(bus_debugger_1_last_addr_out[1]));
  LED led_18 (.in(bus_debugger_1_last_addr_out[0]));
  LED led_19 (.in(bus_debugger_1_last_addr_out[2]));

  // Notes on the sheet:
  //   clk: Hz: 20
endmodule
