// Digital circuit Address Decoder.dig as structural Verilog
module Address_Decoder (
  input  [2:0] ADDR,
  input  [2:0] INPUT,
  output OUT
);

  wire [2:0] xor_1_out;

  assign xor_1_out = ADDR ^ INPUT;  // XOr xor_1, 3 bits wide
  and and_1 (OUT, ~xor_1_out[0], ~xor_1_out[1], ~xor_1_out[2]);  // And
endmodule
