// Digital circuit Bus Controller.dig as structural Verilog
module Bus_Controller (
  input  [15:0] D1,
  input  [2:0] A1,
  input  TB1,
  input  [15:0] D2,
  input  [2:0] A2,
  input  TB2,
  input  [15:0] D3,
  input  [2:0] A3,
  input  TB3,
  input  [15:0] D4,
  input  [2:0] A4,
  input  TB4,
  input  MAIN_CLOCK,
  output FB1,
  output FB2,
  output FB3,
  output FB4
);

  wire address_decoder_1_out, address_decoder_2_out, address_decoder_3_out, address_decoder_4_out, or_1_out,
       or_2_out, or_3_out, or_4_out, or_5_out;
  wire [2:0] driver_1_out;
  wire [15:0] bidirectional_driver_1_dir0;

  Bidirectional_Driver bidirectional_driver_1 (.E(or_1_out), .DIR(FB1), .DIR0(bidirectional_driver_1_dir0), .DIR1(D1));
  assign driver_1_out = TB1 ? A1 : 3'bz;  // Driver driver_1
  or or_1 (or_1_out, FB1, TB1);
  PullDown #(.Bits(16)) pulldown_1 (.out(bidirectional_driver_1_dir0));
  PullDown #(.Bits(3)) pulldown_2 (.out(driver_1_out));
  or or_2 (or_2_out, TB3, TB1, TB2, TB4);
  and and_1 (FB1, ~TB1, or_2_out, address_decoder_1_out);  // And
  Address_Decoder address_decoder_1 (.ADDR(3'b000), .INPUT(driver_1_out), .OUT(address_decoder_1_out));
  Bidirectional_Driver bidirectional_driver_2 (.E(or_3_out), .DIR(FB2), .DIR0(bidirectional_driver_1_dir0), .DIR1(D2));
  assign driver_1_out = TB2 ? A2 : 3'bz;  // Driver driver_2
  or or_3 (or_3_out, FB2, TB2);
  and and_2 (FB2, ~TB2, or_2_out, address_decoder_2_out);  // And
  Address_Decoder address_decoder_2 (.ADDR(3'b001), .INPUT(driver_1_out), .OUT(address_decoder_2_out));
  Bidirectional_Driver bidirectional_driver_3 (.E(or_4_out), .DIR(FB3), .DIR0(bidirectional_driver_1_dir0), .DIR1(D3));
  assign driver_1_out = TB3 ? A3 : 3'bz;  // Driver driver_3
  or or_4 (or_4_out, FB3, TB3);
  and and_3 (FB3, ~TB3, or_2_out, address_decoder_3_out);  // And
  Address_Decoder address_decoder_3 (.ADDR(3'b010), .INPUT(driver_1_out), .OUT(address_decoder_3_out));
  Bidirectional_Driver bidirectional_driver_4 (.E(or_5_out), .DIR(FB4), .DIR0(bidirectional_driver_1_dir0), .DIR1(D4));
  assign driver_1_out = TB4 ? A4 : 3'bz;  // Driver driver_4
  or or_5 (or_5_out, FB4, TB4);
  and and_4 (FB4, ~TB4, or_2_out, address_decoder_4_out);  // And
  Address_Decoder address_decoder_4 (.ADDR(3'b011), .INPUT(driver_1_out), .OUT(address_decoder_4_out));
endmodule
