// Digital circuit 16 Bit Demultiplexer.dig as structural Verilog
module _16_Bit_Demultiplexer (
  input  IN,
  input  [3:0] ADDR,
  output _0,
  output _1,
  output _2,
  output _3,
  output _4,
  output _5,
  output _6,
  output _7,
  output _8,
  output _9,
  output _10,
  output _11,
  output _12,
  output _13,
  output _14,
  output _15
);

  wire demultiplexer_1_out_0, demultiplexer_1_out_1, demultiplexer_2_out_0, demultiplexer_2_out_1,
       demultiplexer_3_out_0, demultiplexer_3_out_1, demultiplexer_4_out_0, demultiplexer_4_out_1,
       demultiplexer_5_out_0, demultiplexer_5_out_1, demultiplexer_6_out_0, demultiplexer_6_out_1,
       demultiplexer_7_out_0, demultiplexer_7_out_1, not_1_out, not_2_out, not_3_out;

  Demultiplexer demultiplexer_1 (.sel(ADDR[0]), .in(IN), .out_0(demultiplexer_1_out_0), .out_1(demultiplexer_1_out_1));
  Demultiplexer demultiplexer_2 (
    .sel(not_1_out), .in(demultiplexer_1_out_0), .out_0(demultiplexer_2_out_0), .out_1(demultiplexer_2_out_1));
  Demultiplexer demultiplexer_3 (
    .sel(ADDR[1]), .in(demultiplexer_1_out_1), .out_0(demultiplexer_3_out_0), .out_1(demultiplexer_3_out_1));
  not not_1 (not_1_out, ADDR[1]);
  not not_2 (not_2_out, ADDR[2]);
  Demultiplexer demultiplexer_4 (
    .sel(not_2_out), .in(demultiplexer_2_out_0), .out_0(demultiplexer_4_out_0), .out_1(demultiplexer_4_out_1));
  Demultiplexer demultiplexer_5 (
    .sel(ADDR[2]), .in(demultiplexer_2_out_1), .out_0(demultiplexer_5_out_0), .out_1(demultiplexer_5_out_1));
  Demultiplexer demultiplexer_6 (
    .sel(not_2_out), .in(demultiplexer_3_out_0), .out_0(demultiplexer_6_out_0), .out_1(demultiplexer_6_out_1));
  Demultiplexer demultiplexer_7 (
    .sel(ADDR[2]), .in(demultiplexer_3_out_1), .out_0(demultiplexer_7_out_0), .out_1(demultiplexer_7_out_1));
  Demultiplexer demultiplexer_8 (.sel(not_3_out), .in(demultiplexer_4_out_0), .out_0(_14), .out_1(_6));
  Demultiplexer demultiplexer_9 (.sel(ADDR[3]), .in(demultiplexer_4_out_1), .out_0(_2), .out_1(_10));
  Demultiplexer demultiplexer_10 (.sel(not_3_out), .in(demultiplexer_5_out_0), .out_0(_8), .out_1(_0));
  Demultiplexer demultiplexer_11 (.sel(ADDR[3]), .in(demultiplexer_5_out_1), .out_0(_4), .out_1(_12));
  Demultiplexer demultiplexer_12 (.sel(not_3_out), .in(demultiplexer_6_out_0), .out_0(_13), .out_1(_5));
  Demultiplexer demultiplexer_13 (.sel(ADDR[3]), .in(demultiplexer_6_out_1), .out_0(_1), .out_1(_9));
  Demultiplexer demultiplexer_14 (.sel(not_3_out), .in(demultiplexer_7_out_0), .out_0(_11), .out_1(_3));
  Demultiplexer demultiplexer_15 (.sel(ADDR[3]), .in(demultiplexer_7_out_1), .out_0(_7), .out_1(_15));
  not not_3 (not_3_out, ADDR[3]);
endmodule
