// Digital circuit Bidirectional Driver.dig as structural Verilog
module Bidirectional_Driver (
  input  E,
  input  DIR,
  output [15:0] DIR0,
  output [15:0] DIR1
);

  wire and_1_out, and_2_out;

  and and_1 (and_1_out, ~DIR, E);  // And
  and and_2 (and_2_out, E, DIR);
  assign DIR0 = and_1_out ? DIR1 : 16'bz;  // Driver driver_1
  assign DIR1 = and_2_out ? DIR0 : 16'bz;  // Driver driver_2
endmodule
