// Digital circuit Bus Debugger.dig as structural Verilog
module Bus_Debugger (
  input  [15:0] DATA,
  input  [2:0] ADDR,
  input  TB,
  input  [15:0] TEST_DATA,
  input  TEST_SEND,
  input  CLK,
  output FB,
  output [15:0] LAST_DATA_OUT,
  output [2:0] LAST_ADDR_OUT
);

  wire and_1_out, delay_1_out, delay_2_out;
  wire [15:0] pulldown_1_out;

  D_FF #(.Bits(16)) d_ff_1 (.D(pulldown_1_out), .C(and_1_out), .Q(LAST_DATA_OUT));  // open: nQ
  PullDown #(.Bits(16)) pulldown_1 (.out(pulldown_1_out));
  D_FF #(.Bits(3)) d_ff_2 (.D(ADDR), .C(and_1_out), .Q(LAST_ADDR_OUT));  // open: nQ
  assign DATA = TEST_SEND ? TEST_DATA : 16'bz;  // Driver driver_1
  assign pulldown_1_out = ~TEST_SEND ? DATA : 16'bz;  // DriverInvSel driverinvsel_1
  and and_1 (and_1_out, CLK, delay_2_out);
  Delay delay_1 (.in(TB), .out(delay_1_out));
  Delay delay_2 (.in(delay_1_out), .out(delay_2_out));

  assign FB = TEST_SEND;
endmodule
