// Digital circuit CPU.dig as structural Verilog
module CPU (
  input  [16:0] PRGMR_A,
  input  PRMGR_ACT,
  input  [7:0] PRMR_DATA,
  input  PRMR_WE,
  input  clk,
  input  [15:0] TEST_DATA,
  input  TEST_SEND,
  input  in_8,
  input  [3:0] in_9
);

  wire _16_bit_or_combinator_1_o, ALU_IF_EN, and_1_out, and_2_out, and_3_out, and_4_out, and_5_out,
       and_7_out, and_8_out, and_10_out, and_11_out, bus_debugger_1_fb, CONT, CONT1, CONT2, CONT2_WE, CONT4,
       CONT5, CONT6, CONT7, CONT_ALU, d_ff_1_q, d_ff_2_nq, d_ff_5_nq, d_ff_6_q, decoder_1_out_0,
       decoder_1_out_1, decoder_1_out_2, decoder_1_out_3, decoder_1_out_4, decoder_2_out_2, decoder_3_out_0,
       decoder_3_out_1, decoder_3_out_2, delay_1_out, delay_2_out, delay_3_out, delay_4_out, IF_EN,
       instruction_decoder_1_halt, instruction_decoder_1_hold, instruction_decoder_1_movez,
       instruction_decoder_1_movnz, instruction_decoder_1_reg_write_enable, or_1_out, or_2_out, or_3_out,
       or_4_out, or_5_out, or_7_out, or_8_out, or_9_out, or_10_out, or_11_out, or_12_out, or_13_out,
       or_15_out, or_16_out, or_17_out, or_18_out, or_19_out, RST, SET_DIV, SET_OVR, xor_1_out;
  wire [0:0] or_6_out;
  wire [1:0] counter_2_out, counter_3_out;
  wire [2:0] ADDR_BUF_q, bus_debugger_1_last_addr_out, counter_1_out;
  wire [3:0] driver_1_out, instruction_decoder_1_reg_if_addr, instruction_decoder_1_reg_read_addr,
       instruction_decoder_1_reg_write_addr, registers_1_h_out_2;
  wire [7:0] GLS29EE010_70_4C_PHE__EEPROM_d, instruction_decoder_1_eq, LOW_INS_q;
  wire [15:0] alu_1_out, bus_debugger_1_last_data_out, d_ff_3_q, d_ff_4_q, DATA_READ, DATA_WRITE,
       driver_2_out, driverinvsel_3_out, PC_OUT, registers_1_h_out;
  wire [15:8] HIGH_INS_q;
  wire [16:0] driverinvsel_4_out;

  or or_1 (or_1_out, IF_EN, ALU_IF_EN);
  assign driver_1_out = or_1_out ? instruction_decoder_1_reg_if_addr : 4'bz;  // Driver driver_1
  assign driver_1_out = ~or_1_out ? instruction_decoder_1_reg_read_addr : 4'bz;  // DriverInvSel driverinvsel_1
  Seven_Seg_Hex seven_seg_hex_1 (.d(PC_OUT[15:12]), .dp(1'b0));
  assign driver_2_out = bus_debugger_1_fb ? driverinvsel_3_out : 16'bz;  // Driver driver_2
  assign in_9 = ~in_8 ? driver_1_out : 4'bz;  // DriverInvSel driverinvsel_2
  Seven_Seg_Hex seven_seg_hex_2 (.d(PC_OUT[11:8]), .dp(1'b0));
  assign driverinvsel_3_out = ~bus_debugger_1_fb ? DATA_READ : 16'bz;  // DriverInvSel driverinvsel_3
  PullDown #(.Bits(4)) pulldown_1 (.out(in_9));
  Registers registers_1 (
    .ADDR_READ(in_9), .ADDR_WRITE(instruction_decoder_1_reg_write_addr), .DATA_WRITE(DATA_WRITE), .CLK(clk),
    .WRITE_ENABLE(or_9_out), .BUS_DATA_IN(driver_2_out), .FROM_BUS_IN(bus_debugger_1_fb), .PC_INC(or_2_out),
    .RESET(RST), .DATA_READ(DATA_READ), .PC_OUT(PC_OUT),
    .H_OUT({registers_1_h_out[15:12], registers_1_h_out_2, registers_1_h_out[7:0]}));
  or or_2 (or_2_out, and_8_out, decoder_1_out_4);
  Seven_Seg_Hex seven_seg_hex_3 (.d(registers_1_h_out[15:12]), .dp(1'b0));
  Seven_Seg_Hex seven_seg_hex_4 (.d(PC_OUT[7:4]), .dp(1'b0));
  Seven_Seg_Hex seven_seg_hex_5 (.d(registers_1_h_out_2), .dp(1'b0));
  D_FF #(.Bits(3)) ADDR_BUF (.D(instruction_decoder_1_reg_write_addr[2:0]), .C(CONT4), .Q(ADDR_BUF_q));  // open: nQ
  Seven_Seg_Hex seven_seg_hex_6 (.d(registers_1_h_out[7:4]), .dp(1'b0));
  Seven_Seg_Hex seven_seg_hex_7 (.d(PC_OUT[3:0]), .dp(1'b0));
  D_FF d_ff_1 (.D(CONT4), .C(~clk), .Q(d_ff_1_q));  // open: nQ
  Seven_Seg_Hex seven_seg_hex_8 (.d(registers_1_h_out[3:0]), .dp(1'b0));
  Bus_Debugger bus_debugger_1 (
    .DATA(driverinvsel_3_out), .ADDR(ADDR_BUF_q), .TB(d_ff_1_q), .TEST_DATA(TEST_DATA),
    .TEST_SEND(TEST_SEND), .CLK(clk), .FB(bus_debugger_1_fb), .LAST_DATA_OUT(bus_debugger_1_last_data_out),
    .LAST_ADDR_OUT(bus_debugger_1_last_addr_out));
  // Probe CLK on clk
  Reset_On_First_Clock reset_on_first_clock_1 (.CLK(clk), .RST(RST));
  assign driverinvsel_4_out = ~PRMGR_ACT ? {PC_OUT, or_6_out[0]} : 17'bz;  // DriverInvSel driverinvsel_4
  PullDown pulldown_2 (.out(PRMGR_ACT));
  or or_3 (or_3_out, RST, decoder_1_out_4);
  LED led_1 (.in(bus_debugger_1_last_data_out[1]));
  LED led_2 (.in(bus_debugger_1_last_data_out[0]));
  LED led_3 (.in(bus_debugger_1_last_data_out[2]));
  or or_4 (or_4_out, decoder_1_out_0, decoder_1_out_1, CONT, decoder_1_out_3);
  Counter #(.Bits(3)) counter_1 (.en(or_4_out), .C(clk), .clr(or_3_out), .out(counter_1_out));  // open: ovf
  assign driverinvsel_4_out = PRMGR_ACT ? PRGMR_A : 17'bz;  // Driver driver_3
  LED led_4 (.in(bus_debugger_1_last_data_out[3]));
  LED led_5 (.in(bus_debugger_1_last_data_out[5]));
  LED led_6 (.in(bus_debugger_1_last_data_out[4]));
  LED led_7 (.in(bus_debugger_1_last_data_out[6]));
  PullDown pulldown_3 (.out(PRMR_WE));
  LED led_8 (.in(bus_debugger_1_last_data_out[7]));
  LED led_9 (.in(bus_debugger_1_last_data_out[9]));
  LED led_10 (.in(bus_debugger_1_last_data_out[8]));
  LED led_11 (.in(bus_debugger_1_last_data_out[10]));
  Decoder #(.Selector_Bits(3)) decoder_1 (
    .sel(counter_1_out), .out_0(decoder_1_out_0), .out_1(decoder_1_out_1), .out_2(decoder_1_out_2),
    .out_3(decoder_1_out_3), .out_4(decoder_1_out_4));  // open: out_5, out_6, out_7
  LED led_12 (.in(bus_debugger_1_last_data_out[11]));
  LED led_13 (.in(bus_debugger_1_last_data_out[13]));
  LED led_14 (.in(bus_debugger_1_last_data_out[12]));
  LED led_15 (.in(bus_debugger_1_last_data_out[14]));
  and and_1 (and_1_out, SET_OVR, ~CONT6);  // And
  or or_5 (or_5_out, decoder_1_out_0, decoder_3_out_1);
  or or_6 (or_6_out[0], decoder_3_out_2, decoder_1_out_1);
  EEPROM #(.AddrBits(17), .Bits(8)) GLS29EE010_70_4C_PHE__EEPROM (
    .A(driverinvsel_4_out), .CS(1'b1), .WE(PRMR_WE), .OE(~PRMGR_ACT), .D(GLS29EE010_70_4C_PHE__EEPROM_d));
  LED led_16 (.in(bus_debugger_1_last_data_out[15]));
  LED led_17 (.in(bus_debugger_1_last_addr_out[0]));
  or or_7 (or_7_out, decoder_1_out_3, RST, decoder_1_out_2);
  LED led_18 (.in(bus_debugger_1_last_addr_out[1]));
  LED led_19 (.in(bus_debugger_1_last_addr_out[2]));
  assign GLS29EE010_70_4C_PHE__EEPROM_d = PRMGR_ACT ? PRMR_DATA : 8'bz;  // Driver driver_4
  D_FF #(.Bits(8)) HIGH_INS (.D(GLS29EE010_70_4C_PHE__EEPROM_d), .C(and_2_out), .Q(HIGH_INS_q));  // open: nQ
  and and_2 (and_2_out, clk, or_5_out);
  and and_3 (and_3_out, or_7_out, ~and_1_out, clk);  // And
  D_FF #(.Bits(8)) LOW_INS (.D(GLS29EE010_70_4C_PHE__EEPROM_d), .C(and_4_out), .Q(LOW_INS_q));  // open: nQ
  Delay delay_1 (.in(and_3_out), .out(delay_1_out));
  Delay delay_2 (.in(delay_3_out), .out(delay_2_out));
  assign DATA_WRITE = SET_DIV ? {HIGH_INS_q, LOW_INS_q} : 16'bz;  // Driver driver_5
  and and_4 (and_4_out, ~clk, or_6_out[0]);  // And
  Delay delay_3 (.in(delay_1_out), .out(delay_3_out));
  Delay delay_4 (.in(delay_2_out), .out(delay_4_out));
  or or_8 (or_8_out, or_10_out, decoder_1_out_3, RST);
  Instruction_Decoder instruction_decoder_1 (
    .INS({HIGH_INS_q, LOW_INS_q}), .SET_CLK(delay_4_out), .CLR(or_8_out), .HALT(instruction_decoder_1_halt),
    .MOV(CONT1), .MOVNZ(instruction_decoder_1_movnz), .MOVEZ(instruction_decoder_1_movez), .BUS(CONT4),
    .HOLD(instruction_decoder_1_hold), .SET(SET_OVR), .RESERVED(CONT7), .AND(instruction_decoder_1_eq[0]),
    .OR(instruction_decoder_1_eq[1]), .NOT(instruction_decoder_1_eq[2]), .ADD(instruction_decoder_1_eq[3]),
    .SHFT(instruction_decoder_1_eq[4]), .MUL(instruction_decoder_1_eq[5]), .GT(instruction_decoder_1_eq[6]),
    .EQ(instruction_decoder_1_eq[7]), .REG_READ_ADDR(instruction_decoder_1_reg_read_addr),
    .REG_WRITE_ADDR(instruction_decoder_1_reg_write_addr), .REG_IF_ADDR(instruction_decoder_1_reg_if_addr),
    .REG_WRITE_ENABLE(instruction_decoder_1_reg_write_enable));  // open: ALU_ENABLE
  or or_9 (or_9_out, decoder_3_out_2, CONT2_WE, CONT1, CONT1, CONT_ALU);
  LED led_20 (.in(instruction_decoder_1_halt));
  assign DATA_WRITE = CONT1 ? DATA_READ : 16'bz;  // Driver driver_6
  and and_5 (and_5_out, instruction_decoder_1_reg_write_enable, ~or_10_out);  // And
  or or_10 (or_10_out, CONT6, decoder_3_out_2);
  and and_6 (CONT5, bus_debugger_1_fb, instruction_decoder_1_hold);
  or or_11 (or_11_out, RST, or_8_out, CONT_ALU);
  or or_12 (or_12_out, RST, CONT6);
  Counter #(.Bits(2)) counter_2 (.en(and_5_out), .C(clk), .clr(or_11_out), .out(counter_2_out));  // open: ovf
  or or_13 (or_13_out, instruction_decoder_1_movez, instruction_decoder_1_movnz);
  Counter #(.Bits(2)) counter_3 (.en(SET_OVR), .C(clk), .clr(or_12_out), .out(counter_3_out));  // open: ovf
  or or_14 (SET_DIV, decoder_3_out_2, CONT6);
  and and_7 (and_7_out, d_ff_5_nq, d_ff_2_nq, or_13_out, ~or_8_out);  // And
  Decoder #(.Selector_Bits(2)) decoder_2 (
    .sel(counter_2_out), .out_1(ALU_IF_EN), .out_2(decoder_2_out_2), .out_3(CONT_ALU));  // open: out_0
  D_FF d_ff_2 (.D(and_7_out), .C(clk), .Q(IF_EN), .nQ(d_ff_2_nq));
  _16_Bit_Or_Combinator _16_bit_or_combinator_1 (.I(DATA_READ), .O(_16_bit_or_combinator_1_o));
  Decoder #(.Selector_Bits(2)) decoder_3 (
    .sel(counter_3_out), .out_0(decoder_3_out_0), .out_1(decoder_3_out_1), .out_2(decoder_3_out_2),
    .out_3(CONT6));
  and and_8 (and_8_out, SET_OVR, decoder_3_out_0);
  D_FF #(.Bits(16)) d_ff_3 (.D(DATA_READ), .C(ALU_IF_EN), .Q(d_ff_3_q));  // open: nQ
  D_FF #(.Bits(16)) d_ff_4 (.D(DATA_READ), .C(decoder_2_out_2), .Q(d_ff_4_q));  // open: nQ
  D_FF d_ff_5 (.D(IF_EN), .C(clk), .Q(CONT2), .nQ(d_ff_5_nq));
  ALU alu_1 (
    .DATA_IN_1(d_ff_3_q), .DATA_IN_2(d_ff_4_q), .F_SEL(instruction_decoder_1_eq),
    .SHFT_IN(instruction_decoder_1_reg_if_addr), .F_SET_CLK(ALU_IF_EN), .OUT(alu_1_out));
  or or_15 (or_15_out, CONT5, CONT4);
  or or_16 (or_16_out, CONT7, CONT6);
  and and_9 (CONT2_WE, d_ff_6_q, CONT2);
  and and_10 (and_10_out, IF_EN, ~clk);  // And
  or or_17 (or_17_out, CONT2, or_15_out);
  or or_18 (or_18_out, or_16_out, CONT_ALU);
  assign DATA_WRITE = CONT_ALU ? alu_1_out : 16'bz;  // Driver driver_7
  D_FF d_ff_6 (.D(_16_bit_or_combinator_1_o), .C(and_10_out), .Q(d_ff_6_q));  // open: nQ
  or or_19 (or_19_out, CONT1, or_18_out);
  xor xor_1 (xor_1_out, d_ff_6_q, instruction_decoder_1_movez);
  or or_20 (CONT, or_17_out, or_19_out);
  and and_11 (and_11_out, CONT2, xor_1_out);
  assign DATA_WRITE = and_11_out ? DATA_READ : 16'bz;  // Driver driver_8

  // Notes on the sheet:
  //   clk: Hz: 50
  //   Program
  //   Counter:
  //   DBG
  //   Register H:
  //   NOTE: REG_ADDR_WRITE is second parameter,
  //   therefore it can be abused as literal for BUS addr.
  //   0: INS_LOAD_LOW
  //   1: INS_LOAD_HIGH
  //   2: WAITING_FOR_INS_EXEC
  //   3: CLEANUP
  //   4: PC_INCREMENT
  //   contents of GLS29EE010_70_4C_PHE__EEPROM (hex, n*v repeats v):
  //   0,d1,1,d1,3,e1,5,6,0,14,12,b,0,11,1,21,7,1,d3,3b,9,6,0,4,38,5e,8b,92
  //   HALTED
  //   MOVNZ
  //   MOVEZ
endmodule
