// Digital circuit Counter.dig as structural Verilog
module Counter (
  input  CLK,
  output _1,
  output _2,
  output _3
);

  wire or_1_out, reset_on_first_clock_1_rst;

  Reset_On_First_Clock reset_on_first_clock_1 (.CLK(CLK), .RST(reset_on_first_clock_1_rst));
  or or_1 (or_1_out, _3, reset_on_first_clock_1_rst);
  D_FF d_ff_1 (.D(or_1_out), .C(CLK), .Q(_1));  // open: nQ
  D_FF d_ff_2 (.D(_1), .C(CLK), .Q(_2));  // open: nQ
  D_FF d_ff_3 (.D(_2), .C(CLK), .Q(_3));  // open: nQ
endmodule
