// Digital circuit MCPCflat.dig as structural Verilog
module MCPCflat (
  input  MAIN_CLOCK,
  input  [16:0] PRGMR_A,
  input  PRMGR_ACT,
  input  [7:0] PRMR_DATA,
  input  PRMR_WE,
  input  in_9,
  output [2:0] out_6,
  output [15:0] out_7,
  output out_8
);

  wire _16_bit_or_combinator_1_o, ALU_IF_EN, and_1_out, and_2_out, and_3_out, and_4_out, and_5_out,
       and_6_out, and_7_out, and_8_out, and_9_out, and_11_out, and_12_out, CONT, CONT1, CONT2, CONT2_WE,
       CONT4, CONT5, CONT6, CONT7, CONT_ALU, d_ff_1_nq, d_ff_2_nq, d_ff_5_nq, d_ff_6_q, decoder_1_out_0,
       decoder_1_out_1, decoder_1_out_2, decoder_1_out_3, decoder_1_out_4, decoder_2_out_2, decoder_3_out_0,
       decoder_3_out_1, decoder_3_out_2, delay_1_out, delay_2_out, delay_3_out, delay_4_out, IF_EN,
       instruction_decoder_1_halt, instruction_decoder_1_movez, instruction_decoder_1_movnz,
       instruction_decoder_1_reg_write_enable, or_1_out, or_2_out, or_3_out, or_4_out, or_6_out, or_7_out,
       or_8_out, or_9_out, or_10_out, or_11_out, or_12_out, or_13_out, or_15_out, or_16_out, or_17_out,
       or_18_out, or_19_out, RST, SET_DIV, SET_OVR, xor_1_out;
  wire [0:0] or_5_out;
  wire [1:0] counter_2_out, counter_3_out;
  wire [2:0] counter_1_out;
  wire [3:0] driver_1_out, instruction_decoder_1_reg_if_addr, instruction_decoder_1_reg_read_addr,
       instruction_decoder_1_reg_write_addr, registers_1_h_out;
  wire [7:0] GLS29EE010_70_4C_PHE__EEPROM_d, instruction_decoder_1_and;
  wire [15:0] alu_1_out, d_ff_3_q, d_ff_4_q, DATA_READ, DATA_WRITE, driver_2_out, LOW_INS_q, PC_OUT;
  wire [15:4] registers_1_h_out_2;
  wire [16:0] driverinvsel_3_out;

  or or_1 (or_1_out, IF_EN, ALU_IF_EN);
  assign driver_1_out = or_1_out ? instruction_decoder_1_reg_if_addr : 4'bz;  // Driver driver_1
  assign driver_1_out = ~or_1_out ? instruction_decoder_1_reg_read_addr : 4'bz;  // DriverInvSel driverinvsel_1
  Seven_Seg_Hex seven_seg_hex_1 (.d(PC_OUT[15:12]), .dp(1'b0));
  Seven_Seg_Hex seven_seg_hex_2 (.d(PC_OUT[11:8]), .dp(1'b0));
  assign driver_2_out = in_9 ? out_7 : 16'bz;  // Driver driver_2
  Seven_Seg_Hex seven_seg_hex_3 (.d(registers_1_h_out_2[15:12]), .dp(1'b0));
  assign out_7 = ~in_9 ? DATA_READ : 16'bz;  // DriverInvSel driverinvsel_2
  Registers registers_1 (
    .ADDR_READ(driver_1_out), .ADDR_WRITE(instruction_decoder_1_reg_write_addr), .DATA_WRITE(DATA_WRITE),
    .CLK(MAIN_CLOCK), .WRITE_ENABLE(or_9_out), .BUS_DATA_IN(driver_2_out), .FROM_BUS_IN(in_9),
    .PC_INC(or_2_out), .RESET(RST), .DATA_READ(DATA_READ), .PC_OUT(PC_OUT),
    .H_OUT({registers_1_h_out_2, registers_1_h_out}));
  or or_2 (or_2_out, and_9_out, decoder_1_out_4);
  Seven_Seg_Hex seven_seg_hex_4 (.d(registers_1_h_out_2[11:8]), .dp(1'b0));
  Seven_Seg_Hex seven_seg_hex_5 (.d(PC_OUT[7:4]), .dp(1'b0));
  D_FF #(.Bits(3)) ADDR_BUF (.D(instruction_decoder_1_reg_write_addr[2:0]), .C(CONT4), .Q(out_6));  // open: nQ
  Seven_Seg_Hex seven_seg_hex_6 (.d(PC_OUT[3:0]), .dp(1'b0));
  Seven_Seg_Hex seven_seg_hex_7 (.d(registers_1_h_out_2[7:4]), .dp(1'b0));
  Seven_Seg_Hex seven_seg_hex_8 (.d(registers_1_h_out), .dp(1'b0));
  and and_1 (and_1_out, d_ff_1_nq, CONT4);
  D_FF d_ff_1 (.D(and_1_out), .C(~MAIN_CLOCK), .Q(out_8), .nQ(d_ff_1_nq));
  assign driverinvsel_3_out = ~PRMGR_ACT ? {PC_OUT, or_5_out[0]} : 17'bz;  // DriverInvSel driverinvsel_3
  PullDown pulldown_1 (.out(PRMGR_ACT));
  or or_3 (or_3_out, RST, decoder_1_out_4);
  or or_4 (or_4_out, decoder_1_out_0, decoder_1_out_1, CONT, decoder_1_out_3);
  Counter #(.Bits(3)) counter_1 (.en(or_4_out), .C(MAIN_CLOCK), .clr(or_3_out), .out(counter_1_out));  // open: ovf
  assign driverinvsel_3_out = PRMGR_ACT ? PRGMR_A : 17'bz;  // Driver driver_3
  PullDown pulldown_2 (.out(PRMR_WE));
  and and_2 (and_2_out, SET_OVR, ~CONT6);  // And
  Decoder #(.Selector_Bits(3)) decoder_1 (
    .sel(counter_1_out), .out_0(decoder_1_out_0), .out_1(decoder_1_out_1), .out_2(decoder_1_out_2),
    .out_3(decoder_1_out_3), .out_4(decoder_1_out_4));  // open: out_5, out_6, out_7
  or or_5 (or_5_out[0], decoder_3_out_2, decoder_1_out_1);
  EEPROM #(.AddrBits(17), .Bits(8)) GLS29EE010_70_4C_PHE__EEPROM (
    .A(driverinvsel_3_out), .CS(1'b1), .WE(PRMR_WE), .OE(~PRMGR_ACT), .D(GLS29EE010_70_4C_PHE__EEPROM_d));
  or or_6 (or_6_out, decoder_1_out_3, RST, decoder_1_out_2);
  or or_7 (or_7_out, decoder_1_out_0, decoder_3_out_1);
  assign GLS29EE010_70_4C_PHE__EEPROM_d = PRMGR_ACT ? PRMR_DATA : 8'bz;  // Driver driver_4
  D_FF #(.Bits(8)) HIGH_INS (.D(GLS29EE010_70_4C_PHE__EEPROM_d), .C(and_3_out), .Q(LOW_INS_q[15:8]));  // open: nQ
  and and_3 (and_3_out, MAIN_CLOCK, or_7_out);
  and and_4 (and_4_out, or_6_out, ~and_2_out, MAIN_CLOCK);  // And
  D_FF #(.Bits(8)) LOW_INS (.D(GLS29EE010_70_4C_PHE__EEPROM_d), .C(and_5_out), .Q(LOW_INS_q[7:0]));  // open: nQ
  Delay delay_1 (.in(and_4_out), .out(delay_1_out));
  Delay delay_2 (.in(delay_3_out), .out(delay_2_out));
  assign DATA_WRITE = SET_DIV ? LOW_INS_q : 16'bz;  // Driver driver_5
  and and_5 (and_5_out, ~MAIN_CLOCK, or_5_out[0]);  // And
  Delay delay_3 (.in(delay_1_out), .out(delay_3_out));
  Delay delay_4 (.in(delay_2_out), .out(delay_4_out));
  or or_8 (or_8_out, or_10_out, decoder_1_out_3, RST);
  and and_6 (and_6_out, ~decoder_1_out_4, ~decoder_1_out_3, CONT1);  // And
  Instruction_Decoder instruction_decoder_1 (
    .INS(LOW_INS_q), .SET_CLK(delay_4_out), .CLR(or_8_out), .HALT(instruction_decoder_1_halt), .MOV(CONT1),
    .MOVNZ(instruction_decoder_1_movnz), .MOVEZ(instruction_decoder_1_movez), .BUS(CONT4), .HOLD(CONT5),
    .SET(SET_OVR), .RESERVED(CONT7), .AND(instruction_decoder_1_and[0]), .OR(instruction_decoder_1_and[1]),
    .NOT(instruction_decoder_1_and[2]), .ADD(instruction_decoder_1_and[3]),
    .SHFT(instruction_decoder_1_and[4]), .MUL(instruction_decoder_1_and[5]),
    .GT(instruction_decoder_1_and[6]), .EQ(instruction_decoder_1_and[7]),
    .REG_READ_ADDR(instruction_decoder_1_reg_read_addr),
    .REG_WRITE_ADDR(instruction_decoder_1_reg_write_addr), .REG_IF_ADDR(instruction_decoder_1_reg_if_addr),
    .REG_WRITE_ENABLE(instruction_decoder_1_reg_write_enable));  // open: ALU_ENABLE
  or or_9 (or_9_out, decoder_3_out_2, CONT2_WE, and_6_out, CONT_ALU);
  LED led_1 (.in(instruction_decoder_1_halt));
  assign DATA_WRITE = CONT1 ? DATA_READ : 16'bz;  // Driver driver_6
  and and_7 (and_7_out, instruction_decoder_1_reg_write_enable, ~or_10_out);  // And
  or or_10 (or_10_out, CONT6, decoder_3_out_2);
  or or_11 (or_11_out, RST, or_8_out, CONT_ALU);
  or or_12 (or_12_out, RST, CONT6);
  Counter #(.Bits(2)) counter_2 (.en(and_7_out), .C(MAIN_CLOCK), .clr(or_11_out), .out(counter_2_out));  // open: ovf
  or or_13 (or_13_out, instruction_decoder_1_movez, instruction_decoder_1_movnz);
  Counter #(.Bits(2)) counter_3 (.en(SET_OVR), .C(MAIN_CLOCK), .clr(or_12_out), .out(counter_3_out));  // open: ovf
  or or_14 (SET_DIV, decoder_3_out_2, CONT6);
  Decoder #(.Selector_Bits(2)) decoder_2 (
    .sel(counter_2_out), .out_1(ALU_IF_EN), .out_2(decoder_2_out_2), .out_3(CONT_ALU));  // open: out_0
  and and_8 (and_8_out, d_ff_5_nq, d_ff_2_nq, or_13_out, ~or_8_out);  // And
  D_FF d_ff_2 (.D(and_8_out), .C(MAIN_CLOCK), .Q(IF_EN), .nQ(d_ff_2_nq));
  _16_Bit_Or_Combinator _16_bit_or_combinator_1 (.I(DATA_READ), .O(_16_bit_or_combinator_1_o));
  Decoder #(.Selector_Bits(2)) decoder_3 (
    .sel(counter_3_out), .out_0(decoder_3_out_0), .out_1(decoder_3_out_1), .out_2(decoder_3_out_2),
    .out_3(CONT6));
  and and_9 (and_9_out, SET_OVR, decoder_3_out_0);
  D_FF #(.Bits(16)) d_ff_3 (.D(DATA_READ), .C(ALU_IF_EN), .Q(d_ff_3_q));  // open: nQ
  D_FF #(.Bits(16)) d_ff_4 (.D(DATA_READ), .C(decoder_2_out_2), .Q(d_ff_4_q));  // open: nQ
  D_FF d_ff_5 (.D(IF_EN), .C(MAIN_CLOCK), .Q(CONT2), .nQ(d_ff_5_nq));
  or or_15 (or_15_out, CONT5, CONT4);
  or or_16 (or_16_out, CONT7, CONT6);
  ALU alu_1 (
    .DATA_IN_1(d_ff_3_q), .DATA_IN_2(d_ff_4_q), .F_SEL(instruction_decoder_1_and),
    .SHFT_IN(instruction_decoder_1_reg_if_addr), .F_SET_CLK(ALU_IF_EN), .OUT(alu_1_out));
  and and_10 (CONT2_WE, xor_1_out, CONT2);
  and and_11 (and_11_out, IF_EN, ~MAIN_CLOCK);  // And
  or or_17 (or_17_out, CONT2, or_15_out);
  or or_18 (or_18_out, or_16_out, CONT_ALU);
  D_FF d_ff_6 (.D(_16_bit_or_combinator_1_o), .C(and_11_out), .Q(d_ff_6_q));  // open: nQ
  or or_19 (or_19_out, CONT1, or_18_out);
  assign DATA_WRITE = CONT_ALU ? alu_1_out : 16'bz;  // Driver driver_7
  xor xor_1 (xor_1_out, d_ff_6_q, instruction_decoder_1_movez);
  or or_20 (CONT, or_17_out, or_19_out);
  and and_12 (and_12_out, CONT2, xor_1_out);
  assign DATA_WRITE = and_12_out ? DATA_READ : 16'bz;  // Driver driver_8
  // Probe CLK on MAIN_CLOCK
  Reset_On_First_Clock reset_on_first_clock_1 (.CLK(MAIN_CLOCK), .RST(RST));

  // Other names for the same wires on the sheet: CLK = MAIN_CLOCK

  // Notes on the sheet:
  //   MAIN_CLOCK: Hz: 50000
  //   PRGMR_A: pin 7
  //   PRMGR_ACT: pin 8
  //   PRMR_DATA: pin 5
  //   PRMR_WE: pin 6
  //   out_6: pin 1
  //   out_7: pin 2
  //   out_8: pin 3
  //   in_9: pin 4
  //   Program
  //   Counter:
  //   DBG
  //   Register H:
  //   NOTE: REG_ADDR_WRITE is second parameter,
  //   therefore it can be abused as literal for BUS addr.
  //   TB
  //   ADDR
  //   DATA
  //   FB
  //   0: INS_LOAD_LOW
  //   1: INS_LOAD_HIGH
  //   2: WAITING_FOR_INS_EXEC
  //   3: CLEANUP
  //   4: PC_INCREMENT
  //   contents of GLS29EE010_70_4C_PHE__EEPROM (hex, n*v repeats v):
  //   a,6,1,ff,6,6,0,8,3,6,ff,0,2,6,0,10,7,21,9,6,65,48,c8,7c,d8,89,1,84,1,94,d7,7b,9,6,
  //   6c,6c,c8,7c,d8,89,1,84,1,94,d7,7b,9,6,2c,6f,c8,7c,d8,89,1,84,1,94,d7,7b,9,6,77,20,
  //   c8,7c,d8,89,1,84,1,94,d7,7b,9,6,72,6f,c8,7c,d8,89,1,84,1,94,d7,7b,9,6,64,6c,c8,7c,
  //   d8,89,1,84,1,94,d7,7b,9,6,a,21,c8,7c,d8,89,1,84,1,94,d7,7b,7,21,4,6,0,17,ea,ab,9,
  //   6,0,54,c8,ac,d8,89,1,84,1,b4,0,7,b,91,da,ab,d7,7b,9,6,0,51,48,7f,8b,93,7,21,d1,1b,
  //   9,6,0,62,68,1f,8b,92,8,6,0,3c,b,81,c8,7c,1,84,0,f1,c5,c,c5,5c,2,54,35,8,2,54,c8,ac,
  //   1,84,8,f1,d8,8b,d8,8b,b,81
  //   HALTED
  //   MOVNZ
  //   MOVEZ
endmodule
