// Digital circuit Registers.dig as structural Verilog
module Registers (
  input  [3:0] ADDR_READ,
  input  [3:0] ADDR_WRITE,
  input  [15:0] DATA_WRITE,
  input  CLK,
  input  WRITE_ENABLE,
  input  [15:0] BUS_DATA_IN,
  input  FROM_BUS_IN,
  input  PC_INC,
  input  RESET,
  output [15:0] DATA_READ,
  output [15:0] PC_OUT,
  output [15:0] H_OUT
);

  wire _16_bit_demultiplexer_1_p3, _16_bit_demultiplexer_1_p4, _16_bit_demultiplexer_1_p5,
       _16_bit_demultiplexer_1_p6, _16_bit_demultiplexer_1_p7, _16_bit_demultiplexer_1_p8,
       _16_bit_demultiplexer_1_p9, _16_bit_demultiplexer_1_p10, _16_bit_demultiplexer_1_p11,
       _16_bit_demultiplexer_1_p12, _16_bit_demultiplexer_1_p13, _16_bit_demultiplexer_1_p14,
       _16_bit_demultiplexer_2_p3, _16_bit_demultiplexer_2_p4, _16_bit_demultiplexer_2_p5,
       _16_bit_demultiplexer_2_p6, _16_bit_demultiplexer_2_p7, _16_bit_demultiplexer_2_p8,
       _16_bit_demultiplexer_2_p9, _16_bit_demultiplexer_2_p10, _16_bit_demultiplexer_2_p11,
       _16_bit_demultiplexer_2_p12, _16_bit_demultiplexer_2_p13, _16_bit_demultiplexer_2_p14,
       _16_bit_demultiplexer_2_p15, _16_bit_demultiplexer_2_p16, _16_bit_demultiplexer_2_p17,
       _16_bit_demultiplexer_2_p18, and_1_out, and_2_out, and_3_out, and_4_out, and_5_out, and_6_out,
       and_7_out, and_8_out, and_9_out, and_10_out, and_11_out, and_12_out, and_13_out, or_1_out, or_2_out;
  wire [15:0] add_1_s, BUS_q, d_ff_1_q, d_ff_2_q, d_ff_3_q, d_ff_4_q, d_ff_5_q, d_ff_6_q, d_ff_7_q, d_ff_9_q,
       driverinvsel_1_out, SCR_q, SP_q;

  // _16_Bit_Demultiplexer _16_bit_demultiplexer_1: pin names not known; wires that end beside it: WRITE_ENABLE, ADDR_WRITE, _16_bit_demultiplexer_1_p3, _16_bit_demultiplexer_1_p4, _16_bit_demultiplexer_1_p5, _16_bit_demultiplexer_1_p6, _16_bit_demultiplexer_1_p7, _16_bit_demultiplexer_1_p8, _16_bit_demultiplexer_1_p9, _16_bit_demultiplexer_1_p10, _16_bit_demultiplexer_1_p11, _16_bit_demultiplexer_1_p12, _16_bit_demultiplexer_1_p13, _16_bit_demultiplexer_1_p14
  or or_1 (or_1_out, RESET, _16_bit_demultiplexer_1_p14);
  // _16_Bit_Demultiplexer _16_bit_demultiplexer_2: pin names not known; wires that end beside it: 1'b1, ADDR_READ, _16_bit_demultiplexer_2_p3, _16_bit_demultiplexer_2_p4, _16_bit_demultiplexer_2_p5, _16_bit_demultiplexer_2_p6, _16_bit_demultiplexer_2_p7, _16_bit_demultiplexer_2_p8, _16_bit_demultiplexer_2_p9, _16_bit_demultiplexer_2_p10, _16_bit_demultiplexer_2_p11, _16_bit_demultiplexer_2_p12, _16_bit_demultiplexer_2_p13, _16_bit_demultiplexer_2_p14, _16_bit_demultiplexer_2_p15, _16_bit_demultiplexer_2_p16, _16_bit_demultiplexer_2_p17, _16_bit_demultiplexer_2_p18
  and and_1 (and_1_out, or_1_out, CLK);
  and and_2 (and_2_out, _16_bit_demultiplexer_1_p3, CLK);
  and and_3 (and_3_out, _16_bit_demultiplexer_1_p4, CLK);
  and and_4 (and_4_out, _16_bit_demultiplexer_1_p5, CLK);
  and and_5 (and_5_out, _16_bit_demultiplexer_1_p6, CLK);
  and and_6 (and_6_out, _16_bit_demultiplexer_1_p7, CLK);
  and and_7 (and_7_out, _16_bit_demultiplexer_1_p8, CLK);
  and and_8 (and_8_out, _16_bit_demultiplexer_1_p9, CLK);
  and and_9 (and_9_out, _16_bit_demultiplexer_1_p10, CLK);
  and and_10 (and_10_out, _16_bit_demultiplexer_1_p11, CLK);
  and and_11 (and_11_out, _16_bit_demultiplexer_1_p12, CLK);
  and and_12 (and_12_out, _16_bit_demultiplexer_1_p13, CLK);
  or or_2 (or_2_out, and_1_out, PC_INC);
  assign driverinvsel_1_out = ~PC_INC ? DATA_WRITE : 16'bz;  // DriverInvSel driverinvsel_1
  assign driverinvsel_1_out = PC_INC ? add_1_s : 16'bz;  // Driver driver_1
  PullDown #(.Bits(16)) pulldown_1 (.out(driverinvsel_1_out));
  D_FF #(.Bits(16)) d_ff_1 (.D(DATA_WRITE), .C(and_2_out), .Q(d_ff_1_q));  // open: nQ
  D_FF #(.Bits(16)) d_ff_2 (.D(DATA_WRITE), .C(and_3_out), .Q(d_ff_2_q));  // open: nQ
  D_FF #(.Bits(16)) d_ff_3 (.D(DATA_WRITE), .C(and_4_out), .Q(d_ff_3_q));  // open: nQ
  D_FF #(.Bits(16)) d_ff_4 (.D(DATA_WRITE), .C(and_5_out), .Q(d_ff_4_q));  // open: nQ
  D_FF #(.Bits(16)) d_ff_5 (.D(DATA_WRITE), .C(and_6_out), .Q(d_ff_5_q));  // open: nQ
  D_FF #(.Bits(16)) d_ff_6 (.D(DATA_WRITE), .C(and_7_out), .Q(d_ff_6_q));  // open: nQ
  D_FF #(.Bits(16)) d_ff_7 (.D(DATA_WRITE), .C(and_8_out), .Q(d_ff_7_q));  // open: nQ
  D_FF #(.Bits(16)) d_ff_8 (.D(DATA_WRITE), .C(and_9_out), .Q(H_OUT));  // open: nQ
  D_FF #(.Bits(16)) d_ff_9 (.D(DATA_WRITE), .C(and_10_out), .Q(d_ff_9_q));  // open: nQ
  D_FF #(.Bits(16)) SCR (.D(DATA_WRITE), .C(and_11_out), .Q(SCR_q));  // open: nQ
  D_FF #(.Bits(16)) SP (.D(DATA_WRITE), .C(and_12_out), .Q(SP_q));  // open: nQ
  D_FF #(.Bits(16)) PC (.D(driverinvsel_1_out), .C(or_2_out), .Q(PC_OUT));  // open: nQ
  Add #(.Bits(16)) add_1 (.a(PC_OUT), .b({16{1'b0}}), .c_i(1'b1), .s(add_1_s));  // open: c_o
  assign DATA_READ = _16_bit_demultiplexer_2_p3 ? d_ff_1_q : 16'bz;  // Driver driver_2
  assign DATA_READ = _16_bit_demultiplexer_2_p4 ? d_ff_2_q : 16'bz;  // Driver driver_3
  assign DATA_READ = _16_bit_demultiplexer_2_p5 ? d_ff_3_q : 16'bz;  // Driver driver_4
  assign DATA_READ = _16_bit_demultiplexer_2_p6 ? d_ff_4_q : 16'bz;  // Driver driver_5
  assign DATA_READ = _16_bit_demultiplexer_2_p7 ? d_ff_5_q : 16'bz;  // Driver driver_6
  assign DATA_READ = _16_bit_demultiplexer_2_p8 ? d_ff_6_q : 16'bz;  // Driver driver_7
  assign DATA_READ = _16_bit_demultiplexer_2_p9 ? d_ff_7_q : 16'bz;  // Driver driver_8
  assign DATA_READ = _16_bit_demultiplexer_2_p10 ? H_OUT : 16'bz;  // Driver driver_9
  assign DATA_READ = _16_bit_demultiplexer_2_p11 ? d_ff_9_q : 16'bz;  // Driver driver_10
  assign DATA_READ = _16_bit_demultiplexer_2_p12 ? SCR_q : 16'bz;  // Driver driver_11
  assign DATA_READ = _16_bit_demultiplexer_2_p13 ? SP_q : 16'bz;  // Driver driver_12
  assign DATA_READ = _16_bit_demultiplexer_2_p14 ? PC_OUT : 16'bz;  // Driver driver_13
  assign DATA_READ = _16_bit_demultiplexer_2_p15 ? {16{1'b0}} : 16'bz;  // Driver driver_14
  assign DATA_READ = _16_bit_demultiplexer_2_p16 ? 16'h1 : 16'bz;  // Driver driver_15
  assign DATA_READ = _16_bit_demultiplexer_2_p17 ? {16{1'b1}} : 16'bz;  // Driver driver_16
  assign DATA_READ = _16_bit_demultiplexer_2_p18 ? BUS_q : 16'bz;  // Driver driver_17
  D_FF #(.Bits(16)) BUS (.D(BUS_DATA_IN), .C(and_13_out), .Q(BUS_q));  // open: nQ
  and and_13 (and_13_out, CLK, FROM_BUS_IN);
endmodule
