// Digital circuit Instruction Decoder.dig as structural Verilog
module Instruction_Decoder (
  input  [15:0] INS,
  input  SET_CLK,
  input  CLR,
  output HALT,
  output MOV,
  output MOVNZ,
  output MOVEZ,
  output BUS,
  output LROM,
  output SET,
  output RESERVED,
  output AND,
  output OR,
  output NOT,
  output ADD,
  output SHFT,
  output MUL,
  output GT,
  output EQ,
  output [3:0] REG_READ_ADDR,
  output [3:0] REG_WRITE_ADDR,
  output [3:0] REG_IF_ADDR,
  output ALU_ENABLE
);

  wire and_1_out, and_2_out, and_3_out, and_4_out, and_5_out, and_6_out, and_7_out, and_8_out, and_9_out,
       and_10_out, decoder_1_out_0, decoder_1_out_1, decoder_1_out_2, decoder_1_out_3, decoder_1_out_4,
       decoder_1_out_5, decoder_1_out_6, decoder_1_out_7, delay_1_out, delay_2_out, delay_3_out, delay_4_out,
       not_1_out;

  D_FF #(.Bits(4)) d_ff_1 (.D(INS[11:8]), .C(SET_CLK), .Q(REG_WRITE_ADDR));  // open: nQ
  and and_1 (and_1_out, and_8_out, decoder_1_out_7);
  D_FF d_ff_2 (.D(and_1_out), .C(SET_CLK), .Q(RESERVED));  // open: nQ
  Decoder #(.Selector_Bits(3)) decoder_1 (
    .sel(INS[2:0]), .out_0(decoder_1_out_0), .out_1(decoder_1_out_1), .out_2(decoder_1_out_2),
    .out_3(decoder_1_out_3), .out_4(decoder_1_out_4), .out_5(decoder_1_out_5), .out_6(decoder_1_out_6),
    .out_7(decoder_1_out_7));
  and and_2 (and_2_out, and_8_out, decoder_1_out_6);
  D_FF d_ff_3 (.D(and_2_out), .C(SET_CLK), .Q(SET));  // open: nQ
  and and_3 (and_3_out, and_8_out, decoder_1_out_5);
  D_FF d_ff_4 (.D(and_3_out), .C(SET_CLK), .Q(LROM));  // open: nQ
  and and_4 (and_4_out, and_8_out, decoder_1_out_4);
  D_FF d_ff_5 (.D(and_4_out), .C(SET_CLK), .Q(BUS));  // open: nQ
  and and_5 (and_5_out, and_8_out, decoder_1_out_3);
  D_FF d_ff_6 (.D(and_5_out), .C(SET_CLK), .Q(MOVEZ));  // open: nQ
  and and_6 (and_6_out, and_8_out, decoder_1_out_2);
  D_FF d_ff_7 (.D(and_6_out), .C(SET_CLK), .Q(MOVNZ));  // open: nQ
  and and_7 (and_7_out, and_8_out, decoder_1_out_1);
  D_FF d_ff_8 (.D(and_7_out), .C(SET_CLK), .Q(MOV));  // open: nQ
  not not_1 (not_1_out, INS[3]);
  and and_8 (and_8_out, not_1_out, ~delay_1_out);  // And
  and and_9 (and_9_out, and_8_out, decoder_1_out_0);
  D_FF d_ff_9 (.D(and_9_out), .C(SET_CLK), .Q(HALT));  // open: nQ
  and and_10 (and_10_out, ~delay_1_out, INS[3]);  // And
  and and_11 (AND, decoder_1_out_0, and_10_out);
  and and_12 (OR, decoder_1_out_1, and_10_out);
  and and_13 (NOT, decoder_1_out_2, and_10_out);
  and and_14 (ADD, decoder_1_out_3, and_10_out);
  and and_15 (SHFT, decoder_1_out_4, and_10_out);
  and and_16 (MUL, decoder_1_out_5, and_10_out);
  and and_17 (GT, decoder_1_out_6, and_10_out);
  and and_18 (EQ, decoder_1_out_7, and_10_out);
  D_FF d_ff_10 (.D(and_10_out), .C(SET_CLK), .Q(ALU_ENABLE));  // open: nQ
  Delay delay_1 (.in(delay_3_out), .out(delay_1_out));
  Delay delay_2 (.in(delay_4_out), .out(delay_2_out));
  Delay delay_3 (.in(delay_2_out), .out(delay_3_out));
  Delay delay_4 (.in(CLR), .out(delay_4_out));

  assign REG_IF_ADDR = INS[15:12];
  assign REG_READ_ADDR = INS[7:4];

  // Notes on the sheet:
  //   ALU BIT
endmodule
