// Digital circuit MCPCcopy.dig as structural Verilog
module MCPCcopy (
  input  [15:0] D4,
  input  [2:0] A4,
  input  TB4,
  input  MAIN_CLOCK,
  input  [16:0] PRGMR_A,
  input  PRMGR_ACT,
  input  [7:0] PRMR_DATA,
  input  PRMR_WE,
  input  in_10,
  input  [3:0] in_11,
  output FB4
);

  wire _16_bit_or_combinator_1_o, address_decoder_1_out, address_decoder_2_out, address_decoder_3_out,
       address_decoder_4_out, ALU_IF_EN, and_1_out, and_2_out, and_3_out, and_4_out, and_5_out, and_6_out,
       and_7_out, and_9_out, and_10_out, and_12_out, and_13_out, and_14_out, and_15_out, and_16_out,
       and_17_out, and_18_out, and_19_out, and_20_out, and_21_out, and_22_out, and_23_out, and_24_out,
       and_25_out, and_26_out, and_27_out, and_28_out, and_29_out, and_30_out, and_31_out, and_32_out,
       and_33_out, and_34_out, and_35_out, CONT, CONT1, CONT2, CONT2_WE, CONT4, CONT5, CONT6, CONT7,
       CONT_ALU, d_ff_1_nq, d_ff_1_q, d_ff_2_nq, d_ff_5_nq, d_ff_6_q, d_ff_9_q, d_ff_10_q, decoder_1_out_0,
       decoder_1_out_1, decoder_1_out_2, decoder_1_out_3, decoder_1_out_4, decoder_2_out_2, decoder_3_out_0,
       decoder_3_out_1, decoder_3_out_2, delay_1_out, delay_2_out, delay_3_out, delay_4_out, delay_5_out,
       delay_6_out, delay_7_out, delay_8_out, delay_9_out, IF_EN, initial_q,
       instruction_decoder_1_alu_enable, instruction_decoder_1_halt, instruction_decoder_1_hold,
       instruction_decoder_1_movez, instruction_decoder_1_movnz, or_1_out, or_2_out, or_3_out, or_4_out,
       or_6_out, or_7_out, or_8_out, or_9_out, or_10_out, or_11_out, or_12_out, or_13_out, or_15_out,
       or_16_out, or_17_out, or_18_out, or_19_out, or_21_out, or_22_out, or_23_out, or_24_out, or_25_out,
       or_26_out, or_28_out, or_29_out, or_30_out, or_31_out, or_32_out, or_33_out, or_34_out, reading1_q,
       reading2_nq, reading2_q, RST, SET_DIV, SET_OVR, writing1_q, writing2_nq, writing2_q, writing3_nq,
       writing3_q, xor_1_out;
  wire [0:0] or_5_out;
  wire [1:0] counter_2_out, counter_3_out;
  wire [2:0] ADDR_BUF_q, ADDR_BUFFER_q, bidirectional_driver_3_dir1_2, counter_1_out, d_ff_11_q,
       driver_9_out, driver_13_out_3, instruction_decoder_1_reg_write_addr;
  wire [3:0] driver_1_out, driver_13_out, instruction_decoder_1_reg_if_addr,
       instruction_decoder_1_reg_read_addr, registers_1_h_out;
  wire [3:3] instruction_decoder_1_reg_write_addr_2;
  wire [7:0] d_ff_8_q, driver_15_out, driver_15_out_2, GLS29EE010_70_4C_PHE__EEPROM_d,
       instruction_decoder_1_and, ramsingleportsel_1_d, READ_BUFFER_q, WRITE_BUFFER_q;
  wire [8:0] d_ff_7_q, driver_13_out_2;
  wire [9:9] or_27_out;
  wire [15:0] alu_1_out, bidirectional_driver_1_dir0, bidirectional_driver_2_dir1,
       bidirectional_driver_3_dir1, d_ff_3_q, d_ff_4_q, DATA_READ, DATA_WRITE, driver_2_out,
       driverinvsel_2_out, keyboard_1_d, LOW_INS_q, PC_OUT;
  wire [15:4] registers_1_h_out_2;
  wire [16:0] driverinvsel_4_out;

  or or_1 (or_1_out, IF_EN, ALU_IF_EN);
  assign driver_1_out = or_1_out ? instruction_decoder_1_reg_if_addr : 4'bz;  // Driver driver_1
  assign driver_1_out = ~or_1_out ? instruction_decoder_1_reg_read_addr : 4'bz;  // DriverInvSel driverinvsel_1
  Seven_Seg_Hex seven_seg_hex_1 (.d(PC_OUT[15:12]), .dp(1'b0));
  Seven_Seg_Hex seven_seg_hex_2 (.d(PC_OUT[11:8]), .dp(1'b0));
  assign driver_2_out = and_19_out ? driverinvsel_2_out : 16'bz;  // Driver driver_2
  assign driverinvsel_2_out = ~and_19_out ? DATA_READ : 16'bz;  // DriverInvSel driverinvsel_2
  PullDown #(.Bits(4)) pulldown_1 (.out(in_11));
  assign in_11 = ~in_10 ? driver_1_out : 4'bz;  // DriverInvSel driverinvsel_3
  Seven_Seg_Hex seven_seg_hex_3 (.d(registers_1_h_out_2[15:12]), .dp(1'b0));
  Registers registers_1 (
    .ADDR_READ(in_11),
    .ADDR_WRITE({instruction_decoder_1_reg_write_addr_2[3], instruction_decoder_1_reg_write_addr}),
    .DATA_WRITE(DATA_WRITE), .CLK(MAIN_CLOCK), .WRITE_ENABLE(or_9_out), .BUS_DATA_IN(driver_2_out),
    .FROM_BUS_IN(and_19_out), .PC_INC(or_2_out), .RESET(RST), .DATA_READ(DATA_READ), .PC_OUT(PC_OUT),
    .H_OUT({registers_1_h_out_2, registers_1_h_out}));
  or or_2 (or_2_out, and_10_out, decoder_1_out_4);
  Seven_Seg_Hex seven_seg_hex_4 (.d(registers_1_h_out_2[11:8]), .dp(1'b0));
  Seven_Seg_Hex seven_seg_hex_5 (.d(PC_OUT[7:4]), .dp(1'b0));
  D_FF #(.Bits(3)) ADDR_BUF (.D(instruction_decoder_1_reg_write_addr), .C(CONT4), .Q(ADDR_BUF_q));  // open: nQ
  Seven_Seg_Hex seven_seg_hex_6 (.d(PC_OUT[3:0]), .dp(1'b0));
  Seven_Seg_Hex seven_seg_hex_7 (.d(registers_1_h_out_2[7:4]), .dp(1'b0));
  Seven_Seg_Hex seven_seg_hex_8 (.d(registers_1_h_out), .dp(1'b0));
  and and_1 (and_1_out, d_ff_1_nq, CONT4);
  D_FF d_ff_1 (.D(and_1_out), .C(~MAIN_CLOCK), .Q(d_ff_1_q), .nQ(d_ff_1_nq));
  assign driverinvsel_4_out = ~PRMGR_ACT ? {PC_OUT, or_5_out[0]} : 17'bz;  // DriverInvSel driverinvsel_4
  PullDown pulldown_2 (.out(PRMGR_ACT));
  or or_3 (or_3_out, RST, decoder_1_out_4);
  or or_4 (or_4_out, decoder_1_out_0, decoder_1_out_1, CONT, decoder_1_out_3);
  Counter #(.Bits(3)) counter_1 (.en(or_4_out), .C(MAIN_CLOCK), .clr(or_3_out), .out(counter_1_out));  // open: ovf
  assign driverinvsel_4_out = PRMGR_ACT ? PRGMR_A : 17'bz;  // Driver driver_3
  PullDown pulldown_3 (.out(PRMR_WE));
  and and_2 (and_2_out, SET_OVR, ~CONT6);  // And
  Decoder #(.Selector_Bits(3)) decoder_1 (
    .sel(counter_1_out), .out_0(decoder_1_out_0), .out_1(decoder_1_out_1), .out_2(decoder_1_out_2),
    .out_3(decoder_1_out_3), .out_4(decoder_1_out_4));  // open: out_5, out_6, out_7
  or or_5 (or_5_out[0], decoder_3_out_2, decoder_1_out_1);
  EEPROM #(.AddrBits(17), .Bits(8)) GLS29EE010_70_4C_PHE__EEPROM (
    .A(driverinvsel_4_out), .CS(1'b1), .WE(PRMR_WE), .OE(~PRMGR_ACT), .D(GLS29EE010_70_4C_PHE__EEPROM_d));
  or or_6 (or_6_out, decoder_1_out_3, RST, decoder_1_out_2);
  or or_7 (or_7_out, decoder_1_out_0, decoder_3_out_1);
  assign GLS29EE010_70_4C_PHE__EEPROM_d = PRMGR_ACT ? PRMR_DATA : 8'bz;  // Driver driver_4
  D_FF #(.Bits(8)) HIGH_INS (.D(GLS29EE010_70_4C_PHE__EEPROM_d), .C(and_3_out), .Q(LOW_INS_q[15:8]));  // open: nQ
  and and_3 (and_3_out, MAIN_CLOCK, or_7_out);
  and and_4 (and_4_out, or_6_out, ~and_2_out, MAIN_CLOCK);  // And
  D_FF #(.Bits(8)) LOW_INS (.D(GLS29EE010_70_4C_PHE__EEPROM_d), .C(and_5_out), .Q(LOW_INS_q[7:0]));  // open: nQ
  Delay delay_1 (.in(and_4_out), .out(delay_1_out));
  Delay delay_2 (.in(delay_3_out), .out(delay_2_out));
  assign DATA_WRITE = SET_DIV ? LOW_INS_q : 16'bz;  // Driver driver_5
  and and_5 (and_5_out, ~MAIN_CLOCK, or_5_out[0]);  // And
  Delay delay_3 (.in(delay_1_out), .out(delay_3_out));
  Delay delay_4 (.in(delay_2_out), .out(delay_4_out));
  or or_8 (or_8_out, or_10_out, decoder_1_out_3, RST);
  and and_6 (and_6_out, ~decoder_1_out_4, ~decoder_1_out_3, CONT1);  // And
  Instruction_Decoder instruction_decoder_1 (
    .INS(LOW_INS_q), .SET_CLK(delay_4_out), .CLR(or_8_out), .HALT(instruction_decoder_1_halt), .MOV(CONT1),
    .MOVNZ(instruction_decoder_1_movnz), .MOVEZ(instruction_decoder_1_movez), .BUS(CONT4),
    .HOLD(instruction_decoder_1_hold), .SET(SET_OVR), .RESERVED(CONT7), .AND(instruction_decoder_1_and[0]),
    .OR(instruction_decoder_1_and[1]), .NOT(instruction_decoder_1_and[2]),
    .ADD(instruction_decoder_1_and[3]), .SHFT(instruction_decoder_1_and[4]),
    .MUL(instruction_decoder_1_and[5]), .GT(instruction_decoder_1_and[6]), .EQ(instruction_decoder_1_and[7]),
    .REG_READ_ADDR(instruction_decoder_1_reg_read_addr),
    .REG_WRITE_ADDR({instruction_decoder_1_reg_write_addr_2[3], instruction_decoder_1_reg_write_addr}),
    .REG_IF_ADDR(instruction_decoder_1_reg_if_addr), .ALU_ENABLE(instruction_decoder_1_alu_enable));
  or or_9 (or_9_out, decoder_3_out_2, CONT2_WE, and_6_out, CONT_ALU);
  LED led_1 (.in(instruction_decoder_1_halt));
  assign DATA_WRITE = CONT1 ? DATA_READ : 16'bz;  // Driver driver_6
  and and_7 (and_7_out, instruction_decoder_1_alu_enable, ~or_10_out);  // And
  Break break_1 (.brk(CONT7));
  or or_10 (or_10_out, CONT6, decoder_3_out_2);
  and and_8 (CONT5, and_19_out, instruction_decoder_1_hold);
  or or_11 (or_11_out, RST, or_8_out, CONT_ALU);
  or or_12 (or_12_out, RST, CONT6);
  Counter #(.Bits(2)) counter_2 (.en(and_7_out), .C(MAIN_CLOCK), .clr(or_11_out), .out(counter_2_out));  // open: ovf
  or or_13 (or_13_out, instruction_decoder_1_movez, instruction_decoder_1_movnz);
  Counter #(.Bits(2)) counter_3 (.en(SET_OVR), .C(MAIN_CLOCK), .clr(or_12_out), .out(counter_3_out));  // open: ovf
  or or_14 (SET_DIV, decoder_3_out_2, CONT6);
  Decoder #(.Selector_Bits(2)) decoder_2 (
    .sel(counter_2_out), .out_1(ALU_IF_EN), .out_2(decoder_2_out_2), .out_3(CONT_ALU));  // open: out_0
  and and_9 (and_9_out, d_ff_5_nq, d_ff_2_nq, or_13_out, ~or_8_out);  // And
  D_FF d_ff_2 (.D(and_9_out), .C(MAIN_CLOCK), .Q(IF_EN), .nQ(d_ff_2_nq));
  _16_Bit_Or_Combinator _16_bit_or_combinator_1 (.I(DATA_READ), .O(_16_bit_or_combinator_1_o));
  Decoder #(.Selector_Bits(2)) decoder_3 (
    .sel(counter_3_out), .out_0(decoder_3_out_0), .out_1(decoder_3_out_1), .out_2(decoder_3_out_2),
    .out_3(CONT6));
  and and_10 (and_10_out, SET_OVR, decoder_3_out_0);
  D_FF #(.Bits(16)) d_ff_3 (.D(DATA_READ), .C(ALU_IF_EN), .Q(d_ff_3_q));  // open: nQ
  D_FF #(.Bits(16)) d_ff_4 (.D(DATA_READ), .C(decoder_2_out_2), .Q(d_ff_4_q));  // open: nQ
  D_FF d_ff_5 (.D(IF_EN), .C(MAIN_CLOCK), .Q(CONT2), .nQ(d_ff_5_nq));
  or or_15 (or_15_out, CONT5, CONT4);
  or or_16 (or_16_out, CONT7, CONT6);
  ALU alu_1 (
    .DATA_IN_1(d_ff_3_q), .DATA_IN_2(d_ff_4_q), .F_SEL(instruction_decoder_1_and),
    .SHFT_IN(instruction_decoder_1_reg_if_addr), .F_SET_CLK(ALU_IF_EN), .OUT(alu_1_out));
  and and_11 (CONT2_WE, xor_1_out, CONT2);
  and and_12 (and_12_out, IF_EN, ~MAIN_CLOCK);  // And
  or or_17 (or_17_out, CONT2, or_15_out);
  or or_18 (or_18_out, or_16_out, CONT_ALU);
  D_FF d_ff_6 (.D(_16_bit_or_combinator_1_o), .C(and_12_out), .Q(d_ff_6_q));  // open: nQ
  or or_19 (or_19_out, CONT1, or_18_out);
  assign DATA_WRITE = CONT_ALU ? alu_1_out : 16'bz;  // Driver driver_7
  xor xor_1 (xor_1_out, d_ff_6_q, instruction_decoder_1_movez);
  or or_20 (CONT, or_17_out, or_19_out);
  and and_13 (and_13_out, CONT2, xor_1_out);
  assign DATA_WRITE = and_13_out ? DATA_READ : 16'bz;  // Driver driver_8
  Bidirectional_Driver bidirectional_driver_1 (
    .E(or_21_out), .DIR(and_19_out), .DIR0(bidirectional_driver_1_dir0), .DIR1(driverinvsel_2_out));
  PullDown #(.Bits(16)) pulldown_4 (.out(bidirectional_driver_1_dir0));
  D_FF writing3 (.D(and_14_out), .C(MAIN_CLOCK), .Q(writing3_q), .nQ(writing3_nq));
  D_FF writing2 (.D(and_17_out), .C(MAIN_CLOCK), .Q(writing2_q), .nQ(writing2_nq));
  D_FF writing1 (.D(and_16_out), .C(and_15_out), .Q(writing1_q));  // open: nQ
  assign driver_9_out = d_ff_1_q ? ADDR_BUF_q : 3'bz;  // Driver driver_9
  or or_21 (or_21_out, and_19_out, d_ff_1_q);
  PullDown #(.Bits(3)) pulldown_5 (.out(driver_9_out));
  and and_14 (and_14_out, writing3_nq, writing2_q);
  and and_15 (and_15_out, MAIN_CLOCK, or_23_out);
  and and_16 (and_16_out, initial_q, ~RST, driver_13_out[0]);  // And
  or or_22 (or_22_out, d_ff_9_q, d_ff_1_q, and_29_out, TB4);
  and and_17 (and_17_out, writing2_nq, and_30_out, writing1_q);
  or or_23 (or_23_out, RST, and_30_out);
  and and_18 (and_18_out, MAIN_CLOCK, and_24_out, ~writing1_q, ~writing2_q, ~writing3_q);  // And
  or or_24 (or_24_out, writing3_q, reading2_q);
  D_FF reading2 (.D(and_20_out), .C(MAIN_CLOCK), .Q(reading2_q), .nQ(reading2_nq));
  D_FF reading1 (.D(and_22_out), .C(and_21_out), .Q(reading1_q));  // open: nQ
  D_FF \initial  (.D(or_25_out), .C(and_23_out), .Q(initial_q));  // open: nQ
  and and_19 (and_19_out, ~d_ff_1_q, or_22_out, address_decoder_1_out);  // And
  and and_20 (and_20_out, reading2_nq, reading1_q);
  and and_21 (and_21_out, or_28_out, MAIN_CLOCK);
  and and_22 (and_22_out, initial_q, ~RST, ~driver_13_out[0]);  // And
  and and_23 (and_23_out, or_26_out, MAIN_CLOCK);
  or or_25 (or_25_out, or_24_out, RST);
  D_FF #(.Bits(9)) d_ff_7 (.D(driver_13_out_2), .C(and_18_out), .Q(d_ff_7_q));  // open: nQ
  or or_26 (or_26_out, or_24_out, RST, and_24_out);
  Address_Decoder address_decoder_1 (.ADDR(3'b000), .INPUT(driver_9_out), .OUT(address_decoder_1_out));
  or or_27 (or_27_out[9], reading2_q, writing3_q);
  or or_28 (or_28_out, reading1_q, RST, and_24_out);
  or or_29 (or_29_out, writing2_q, writing3_q, writing1_q);
  Bidirectional_Driver bidirectional_driver_2 (
    .E(or_31_out), .DIR(and_30_out), .DIR0(bidirectional_driver_1_dir0), .DIR1(bidirectional_driver_2_dir1));
  // Probe CLK on MAIN_CLOCK
  Reset_On_First_Clock reset_on_first_clock_1 (.CLK(MAIN_CLOCK), .RST(RST));
  Delay delay_5 (.in(delay_6_out), .out(delay_5_out));
  or or_30 (or_30_out, delay_5_out, writing3_q);
  RAMSinglePortSel #(.AddrBits(10), .Bits(8)) ramsingleportsel_1 (
    .A({or_27_out[9], d_ff_7_q}), .CS(1'b1), .WE(or_30_out), .OE(~or_29_out), .D(ramsingleportsel_1_d));
  Delay delay_6 (.in(delay_7_out), .out(delay_6_out));
  Delay delay_7 (.in(delay_8_out), .out(delay_7_out));
  assign ramsingleportsel_1_d = writing3_q ? WRITE_BUFFER_q : 8'bz;  // Driver driver_10
  D_FF #(.Bits(8)) WRITE_BUFFER (.D(driver_15_out_2), .C(and_25_out), .Q(WRITE_BUFFER_q));  // open: nQ
  and and_24 (and_24_out, ~writing1_q, and_30_out);  // And
  or or_31 (or_31_out, and_30_out, and_29_out);
  Delay delay_8 (.in(delay_9_out), .out(delay_8_out));
  Delay delay_9 (.in(and_26_out), .out(delay_9_out));
  assign ramsingleportsel_1_d = writing2_q ? d_ff_8_q : 8'bz;  // Driver driver_11
  D_FF #(.Bits(8)) d_ff_8 (.D(driver_15_out), .C(and_25_out), .Q(d_ff_8_q));  // open: nQ
  and and_25 (and_25_out, and_30_out, MAIN_CLOCK);
  assign driver_9_out = and_29_out ? ADDR_BUFFER_q : 3'bz;  // Driver driver_12
  and and_26 (and_26_out, and_30_out, MAIN_CLOCK);
  and and_27 (and_27_out, ~MAIN_CLOCK, reading1_q);  // And
  and and_28 (and_28_out, MAIN_CLOCK, and_24_out, ~writing3_q, ~writing2_q);  // And
  D_FF #(.Bits(3)) ADDR_BUFFER (.D(driver_13_out_3), .C(and_28_out), .Q(ADDR_BUFFER_q));  // open: nQ
  and and_29 (and_29_out, ~MAIN_CLOCK, or_24_out);  // And
  and and_30 (and_30_out, ~and_29_out, or_22_out, address_decoder_2_out);  // And
  PullDown #(.Bits(8)) pulldown_6 (.out(ramsingleportsel_1_d));
  D_FF #(.Bits(8)) READ_BUFFER (.D(ramsingleportsel_1_d), .C(and_27_out), .Q(READ_BUFFER_q));  // open: nQ
  and and_31 (and_31_out, ~or_24_out, ~writing1_q);  // And
  or or_32 (or_32_out, writing1_q, writing2_q);
  Address_Decoder address_decoder_2 (.ADDR(3'b001), .INPUT(driver_9_out), .OUT(address_decoder_2_out));
  assign {driver_13_out_3, driver_13_out_2, driver_13_out} = and_31_out ? bidirectional_driver_2_dir1 : 16'bz;  // Driver driver_13
  and and_32 (and_32_out, or_32_out, ~or_24_out);  // And
  assign bidirectional_driver_2_dir1 = or_24_out ? {ramsingleportsel_1_d, READ_BUFFER_q} : 16'bz;  // Driver driver_14
  assign {driver_15_out_2, driver_15_out} = and_32_out ? bidirectional_driver_2_dir1 : 16'bz;  // Driver driver_15
  Bidirectional_Driver bidirectional_driver_3 (
    .E(or_33_out), .DIR(and_35_out), .DIR0(bidirectional_driver_1_dir0),
    .DIR1({bidirectional_driver_3_dir1[15:4], bidirectional_driver_3_dir1_2, bidirectional_driver_3_dir1[0]}));
  PullDown pulldown_7 (.out(driver_13_out[0]));
  Keyboard keyboard_1 (.C(d_ff_10_q), .D(keyboard_1_d));  // open: en, av
  D_FF d_ff_9 (.D(d_ff_10_q), .C(~MAIN_CLOCK), .Q(d_ff_9_q));  // open: nQ
  assign {bidirectional_driver_3_dir1[15:4], bidirectional_driver_3_dir1_2, bidirectional_driver_3_dir1[0]} = d_ff_9_q ? keyboard_1_d : 16'bz;  // Driver driver_16
  D_FF d_ff_10 (.D(and_33_out), .C(MAIN_CLOCK), .Q(d_ff_10_q));  // open: nQ
  assign driver_9_out = d_ff_9_q ? d_ff_11_q : 3'bz;  // Driver driver_17
  or or_33 (or_33_out, and_35_out, d_ff_9_q);
  and and_33 (and_33_out, ~RST, bidirectional_driver_3_dir1[0]);  // And
  Terminal #(.termWidth(80)) terminal_1 (.D(bidirectional_driver_3_dir1[15:8]), .C(and_34_out));  // open: en
  D_FF #(.Bits(3)) d_ff_11 (.D(bidirectional_driver_3_dir1_2), .C(and_33_out), .Q(d_ff_11_q));  // open: nQ
  and and_34 (and_34_out, ~bidirectional_driver_3_dir1[0], and_35_out, MAIN_CLOCK);  // And
  and and_35 (and_35_out, ~d_ff_9_q, or_22_out, address_decoder_3_out);  // And
  Address_Decoder address_decoder_3 (.ADDR(3'b010), .INPUT(driver_9_out), .OUT(address_decoder_3_out));
  Bidirectional_Driver bidirectional_driver_4 (.E(or_34_out), .DIR(FB4), .DIR0(bidirectional_driver_1_dir0), .DIR1(D4));
  assign driver_9_out = TB4 ? A4 : 3'bz;  // Driver driver_18
  or or_34 (or_34_out, FB4, TB4);
  and and_36 (FB4, ~TB4, or_22_out, address_decoder_4_out);  // And
  Address_Decoder address_decoder_4 (.ADDR(3'b011), .INPUT(driver_9_out), .OUT(address_decoder_4_out));

  // Other names for the same wires on the sheet: CLK = MAIN_CLOCK

  // Notes on the sheet:
  //   MAIN_CLOCK: Hz: 5000
  //   Program
  //   Counter:
  //   DBG
  //   Register H:
  //   NOTE: REG_ADDR_WRITE is second parameter,
  //   therefore it can be abused as literal for BUS addr.
  //   TB
  //   ADDR
  //   DATA
  //   FB
  //   0: INS_LOAD_LOW
  //   1: INS_LOAD_HIGH
  //   2: WAITING_FOR_INS_EXEC
  //   3: CLEANUP
  //   4: PC_INCREMENT
  //   contents of GLS29EE010_70_4C_PHE__EEPROM (hex, n*v repeats v):
  //   a,6,1,ff,6,6,0,8,3,6,ff,0,2,6,0,10,7,21,9,6,65,48,c8,7c,d8,89,1,84,1,94,d7,7b,9,6,
  //   6c,6c,c8,7c,d8,89,1,84,1,94,d7,7b,9,6,2c,6f,c8,7c,d8,89,1,84,1,94,d7,7b,9,6,77,20,
  //   c8,7c,d8,89,1,84,1,94,d7,7b,9,6,72,6f,c8,7c,d8,89,1,84,1,94,d7,7b,9,6,64,6c,c8,7c,
  //   d8,89,1,84,1,94,d7,7b,9,6,a,21,c8,7c,d8,89,1,84,1,94,d7,7b,7,21,4,6,0,17,ea,ab,9,
  //   6,0,54,c8,ac,d8,89,1,84,1,b4,0,7,b,91,da,ab,d7,7b,9,6,0,51,48,7f,8b,93,7,21,d1,1b,
  //   9,6,0,62,68,1f,8b,92,8,6,0,3c,b,81,c8,7c,1,84,0,f1,c5,c,c5,5c,2,54,35,8,2,54,c8,ac,
  //   1,84,8,f1,d8,8b,d8,8b,b,81
  //   HALTED
  //   MOVNZ
  //   MOVEZ
  //   STATE REGISTERS
  //   TB
  //   HIGH-ADDR
  //   FB cutoff
  //   on write
  //   IDT6116 allows write during WE,
  //   not just on rising edge
  //   Delay not needed IRL
endmodule
