// Digital circuit MCPCflat.dig as structural Verilog
module MCPCflat (
  input  [15:0] D4,
  input  [2:0] A4,
  input  TB4,
  input  MAIN_CLOCK,
  input  [16:0] PRGMR_A,
  input  PRMGR_ACT,
  input  [7:0] PRMR_DATA,
  input  PRMR_WE,
  input  in_10,
  input  [3:0] in_11,
  output FB4
);

  wire ALU_IF_EN, and_1_out, and_2_out, and_3_out, and_4_out, and_5_out, and_6_out, and_7_out, and_8_out,
       and_9_out, and_10_out, and_11_out, and_12_out, and_13_out, and_14_out, and_15_out, and_16_out,
       and_17_out, and_18_out, and_19_out, and_20_out, and_21_out, and_22_out, and_23_out, and_24_out,
       and_25_out, and_26_out, and_27_out, and_36_out, and_37_out, and_38_out, and_39_out, and_40_out,
       and_41_out, and_43_out, and_44_out, and_45_out, and_46_out, and_47_out, and_49_out, and_50_out,
       and_51_out, and_52_out, and_53_out, and_54_out, and_55_out, and_56_out, and_57_out, and_58_out,
       and_59_out, and_60_out, and_61_out, and_62_out, and_63_out, and_65_out, and_66_out, and_67_out,
       and_68_out, and_69_out, and_70_out, and_71_out, and_72_out, and_73_out, and_74_out, and_75_out,
       and_76_out, and_77_out, and_78_out, and_79_out, and_80_out, and_81_out, and_82_out, and_84_out,
       comparator_1_eq, comparator_1_gt, CONT, CONT1, CONT2, CONT2_WE, CONT4, CONT5, CONT6, CONT7, CONT_ALU,
       d_ff_10_nq, d_ff_10_q, d_ff_16_q, d_ff_17_q, d_ff_19_q, d_ff_20_q, d_ff_21_nq, d_ff_24_nq, d_ff_25_q,
       d_ff_29_q, d_ff_30_q, decoder_1_out_0, decoder_1_out_1, decoder_1_out_2, decoder_1_out_3,
       decoder_1_out_4, decoder_2_out_0, decoder_2_out_1, decoder_2_out_2, decoder_2_out_3, decoder_2_out_4,
       decoder_2_out_5, decoder_2_out_6, decoder_2_out_7, decoder_3_out_2, decoder_4_out_0, decoder_4_out_1,
       decoder_4_out_2, delay_1_out, delay_2_out, delay_3_out, delay_4_out, delay_5_out, delay_6_out,
       delay_7_out, delay_8_out, delay_9_out, delay_10_out, delay_11_out, delay_12_out, delay_13_out,
       demultiplexer_1_out_0, demultiplexer_1_out_1, demultiplexer_1_out_2, demultiplexer_1_out_3,
       demultiplexer_1_out_4, demultiplexer_1_out_5, demultiplexer_1_out_6, demultiplexer_1_out_7,
       demultiplexer_1_out_8, demultiplexer_1_out_9, demultiplexer_1_out_10, demultiplexer_1_out_11,
       demultiplexer_2_out_0, demultiplexer_2_out_1, demultiplexer_2_out_2, demultiplexer_2_out_3,
       demultiplexer_2_out_4, demultiplexer_2_out_5, demultiplexer_2_out_6, demultiplexer_2_out_7,
       demultiplexer_2_out_8, demultiplexer_2_out_9, demultiplexer_2_out_10, demultiplexer_2_out_11,
       demultiplexer_2_out_12, demultiplexer_2_out_13, demultiplexer_2_out_14, demultiplexer_2_out_15, IF_EN,
       initial_q, not_1_out, not_3_out, or_1_out, or_2_out, or_3_out, or_4_out, or_5_out, or_6_out, or_7_out,
       or_9_out, or_10_out, or_11_out, or_12_out, or_13_out, or_14_out, or_15_out, or_17_out, or_18_out,
       or_19_out, or_20_out, or_21_out, or_22_out, or_24_out, or_26_out, or_27_out, or_28_out, or_29_out,
       or_30_out, or_32_out, or_33_out, or_34_out, or_35_out, or_36_out, or_37_out, or_38_out, or_39_out,
       or_40_out, reading1_q, reading2_nq, reading2_q, reset_1_out, RST, SET_DIV, SET_OVR, writing1_q,
       writing2_nq, writing2_q, writing3_nq, writing3_q, xor_1_out;
  wire [0:0] or_8_out;
  wire [1:0] counter_2_out, counter_3_out, counter_4_out;
  wire [2:0] ADDR_BUF_q, ADDR_BUFFER_q, counter_1_out, d_ff_31_q, driver_36_out, driver_42_out_3,
       driver_46_out_2, xor_2_out, xor_3_out, xor_4_out;
  wire [3:0] d_ff_8_q, d_ff_8_q_2, d_ff_8_q_3, d_ff_8_q_4, d_ff_11_q, driver_18_out, driver_42_out;
  wire [7:0] and_35_out, d_ff_26_q, d_ff_28_q, driver_45_out, driver_45_out_2, driver_46_out,
       driver_46_out_3, GLS29EE010_70_4C_PHE__EEPROM_d, ramsingleportsel_1_d, READ_BUFFER_q, WRITE_BUFFER_q;
  wire [8:0] d_ff_27_q, driver_42_out_2;
  wire [9:9] or_31_out;
  wire [15:0] add_1_s, add_2_s, and_48_out, barrelshifter_1_out, barrelshifter_2_out, BUS_q, d_ff_1_q,
       d_ff_2_q, d_ff_3_q, d_ff_4_q, d_ff_5_q, d_ff_6_q, d_ff_7_q, d_ff_9_q, d_ff_22_q, d_ff_23_q, DATA_READ,
       DATA_WRITE, driver_19_out, driver_26_out, driver_33_out, driver_35_out, driver_38_out,
       driverinvsel_1_out, driverinvsel_4_out, keyboard_1_d, LOW_INS_q, not_2_out, or_25_out, PC_OUT, SCR_q,
       SP_q;
  wire [16:0] driverinvsel_5_out;
  wire [31:0] mul_1_mul;

  Demultiplexer #(.Selector_Bits(4)) demultiplexer_1 (
    .sel(d_ff_11_q), .in(or_11_out), .out_0(demultiplexer_1_out_0), .out_1(demultiplexer_1_out_1),
    .out_2(demultiplexer_1_out_2), .out_3(demultiplexer_1_out_3), .out_4(demultiplexer_1_out_4),
    .out_5(demultiplexer_1_out_5), .out_6(demultiplexer_1_out_6), .out_7(demultiplexer_1_out_7),
    .out_8(demultiplexer_1_out_8), .out_9(demultiplexer_1_out_9), .out_10(demultiplexer_1_out_10),
    .out_11(demultiplexer_1_out_11));  // open: out_12, out_13, out_14, out_15
  or or_1 (or_1_out, RST, demultiplexer_1_out_11);
  Demultiplexer #(.Selector_Bits(4)) demultiplexer_2 (
    .sel(in_11), .in(1'b1), .out_0(demultiplexer_2_out_0), .out_1(demultiplexer_2_out_1),
    .out_2(demultiplexer_2_out_2), .out_3(demultiplexer_2_out_3), .out_4(demultiplexer_2_out_4),
    .out_5(demultiplexer_2_out_5), .out_6(demultiplexer_2_out_6), .out_7(demultiplexer_2_out_7),
    .out_8(demultiplexer_2_out_8), .out_9(demultiplexer_2_out_9), .out_10(demultiplexer_2_out_10),
    .out_11(demultiplexer_2_out_11), .out_12(demultiplexer_2_out_12), .out_13(demultiplexer_2_out_13),
    .out_14(demultiplexer_2_out_14), .out_15(demultiplexer_2_out_15));
  and and_1 (and_1_out, or_1_out, MAIN_CLOCK);
  and and_2 (and_2_out, demultiplexer_1_out_0, MAIN_CLOCK);
  and and_3 (and_3_out, demultiplexer_1_out_1, MAIN_CLOCK);
  and and_4 (and_4_out, demultiplexer_1_out_2, MAIN_CLOCK);
  and and_5 (and_5_out, demultiplexer_1_out_3, MAIN_CLOCK);
  and and_6 (and_6_out, demultiplexer_1_out_4, MAIN_CLOCK);
  and and_7 (and_7_out, demultiplexer_1_out_5, MAIN_CLOCK);
  and and_8 (and_8_out, demultiplexer_1_out_6, MAIN_CLOCK);
  and and_9 (and_9_out, demultiplexer_1_out_7, MAIN_CLOCK);
  and and_10 (and_10_out, demultiplexer_1_out_8, MAIN_CLOCK);
  and and_11 (and_11_out, demultiplexer_1_out_9, MAIN_CLOCK);
  and and_12 (and_12_out, demultiplexer_1_out_10, MAIN_CLOCK);
  or or_2 (or_2_out, and_1_out, or_4_out);
  assign driverinvsel_1_out = ~or_4_out ? DATA_WRITE : 16'bz;  // DriverInvSel driverinvsel_1
  assign driverinvsel_1_out = or_4_out ? add_1_s : 16'bz;  // Driver driver_1
  PullDown #(.Bits(16)) pulldown_1 (.out(driverinvsel_1_out));
  D_FF #(.Bits(16)) d_ff_1 (.D(DATA_WRITE), .C(and_2_out), .Q(d_ff_1_q));  // open: nQ
  D_FF #(.Bits(16)) d_ff_2 (.D(DATA_WRITE), .C(and_3_out), .Q(d_ff_2_q));  // open: nQ
  D_FF #(.Bits(16)) d_ff_3 (.D(DATA_WRITE), .C(and_4_out), .Q(d_ff_3_q));  // open: nQ
  D_FF #(.Bits(16)) d_ff_4 (.D(DATA_WRITE), .C(and_5_out), .Q(d_ff_4_q));  // open: nQ
  D_FF #(.Bits(16)) d_ff_5 (.D(DATA_WRITE), .C(and_6_out), .Q(d_ff_5_q));  // open: nQ
  D_FF #(.Bits(16)) d_ff_6 (.D(DATA_WRITE), .C(and_7_out), .Q(d_ff_6_q));  // open: nQ
  D_FF #(.Bits(16)) d_ff_7 (.D(DATA_WRITE), .C(and_8_out), .Q(d_ff_7_q));  // open: nQ
  D_FF #(.Bits(16)) d_ff_8 (
    .D(DATA_WRITE), .C(and_9_out), .Q({d_ff_8_q_4, d_ff_8_q_3, d_ff_8_q_2, d_ff_8_q}));  // open: nQ
  D_FF #(.Bits(16)) d_ff_9 (.D(DATA_WRITE), .C(and_10_out), .Q(d_ff_9_q));  // open: nQ
  D_FF #(.Bits(16)) SCR (.D(DATA_WRITE), .C(and_11_out), .Q(SCR_q));  // open: nQ
  D_FF #(.Bits(16)) SP (.D(DATA_WRITE), .C(and_12_out), .Q(SP_q));  // open: nQ
  D_FF #(.Bits(16)) PC (.D(driverinvsel_1_out), .C(or_2_out), .Q(PC_OUT));  // open: nQ
  Add #(.Bits(16)) add_1 (.a(PC_OUT), .b({16{1'b0}}), .c_i(1'b1), .s(add_1_s));  // open: c_o
  assign DATA_READ = demultiplexer_2_out_0 ? d_ff_1_q : 16'bz;  // Driver driver_2
  assign DATA_READ = demultiplexer_2_out_1 ? d_ff_2_q : 16'bz;  // Driver driver_3
  assign DATA_READ = demultiplexer_2_out_2 ? d_ff_3_q : 16'bz;  // Driver driver_4
  assign DATA_READ = demultiplexer_2_out_3 ? d_ff_4_q : 16'bz;  // Driver driver_5
  assign DATA_READ = demultiplexer_2_out_4 ? d_ff_5_q : 16'bz;  // Driver driver_6
  assign DATA_READ = demultiplexer_2_out_5 ? d_ff_6_q : 16'bz;  // Driver driver_7
  assign DATA_READ = demultiplexer_2_out_6 ? d_ff_7_q : 16'bz;  // Driver driver_8
  assign DATA_READ = demultiplexer_2_out_7 ? {d_ff_8_q_4, d_ff_8_q_3, d_ff_8_q_2, d_ff_8_q} : 16'bz;  // Driver driver_9
  assign DATA_READ = demultiplexer_2_out_8 ? d_ff_9_q : 16'bz;  // Driver driver_10
  assign DATA_READ = demultiplexer_2_out_9 ? SCR_q : 16'bz;  // Driver driver_11
  assign DATA_READ = demultiplexer_2_out_10 ? SP_q : 16'bz;  // Driver driver_12
  assign DATA_READ = demultiplexer_2_out_11 ? PC_OUT : 16'bz;  // Driver driver_13
  assign DATA_READ = demultiplexer_2_out_12 ? {16{1'b0}} : 16'bz;  // Driver driver_14
  assign DATA_READ = demultiplexer_2_out_13 ? 16'h1 : 16'bz;  // Driver driver_15
  assign DATA_READ = demultiplexer_2_out_14 ? {16{1'b1}} : 16'bz;  // Driver driver_16
  assign DATA_READ = demultiplexer_2_out_15 ? BUS_q : 16'bz;  // Driver driver_17
  D_FF #(.Bits(16)) BUS (.D(driver_19_out), .C(and_13_out), .Q(BUS_q));  // open: nQ
  and and_13 (and_13_out, MAIN_CLOCK, and_53_out);
  or or_3 (or_3_out, IF_EN, ALU_IF_EN);
  assign driver_18_out = or_3_out ? LOW_INS_q[15:12] : 4'bz;  // Driver driver_18
  assign driver_18_out = ~or_3_out ? LOW_INS_q[7:4] : 4'bz;  // DriverInvSel driverinvsel_2
  Seven_Seg_Hex seven_seg_hex_1 (.d(PC_OUT[15:12]), .dp(1'b0));
  assign driver_19_out = and_53_out ? driverinvsel_4_out : 16'bz;  // Driver driver_19
  assign in_11 = ~in_10 ? driver_18_out : 4'bz;  // DriverInvSel driverinvsel_3
  Seven_Seg_Hex seven_seg_hex_2 (.d(PC_OUT[11:8]), .dp(1'b0));
  assign driverinvsel_4_out = ~and_53_out ? DATA_READ : 16'bz;  // DriverInvSel driverinvsel_4
  PullDown #(.Bits(4)) pulldown_2 (.out(in_11));
  or or_4 (or_4_out, and_40_out, decoder_1_out_4);
  Seven_Seg_Hex seven_seg_hex_3 (.d(d_ff_8_q_4), .dp(1'b0));
  Seven_Seg_Hex seven_seg_hex_4 (.d(PC_OUT[7:4]), .dp(1'b0));
  Seven_Seg_Hex seven_seg_hex_5 (.d(d_ff_8_q_3), .dp(1'b0));
  D_FF #(.Bits(3)) ADDR_BUF (.D(d_ff_11_q[2:0]), .C(CONT4), .Q(ADDR_BUF_q));  // open: nQ
  Seven_Seg_Hex seven_seg_hex_6 (.d(d_ff_8_q_2), .dp(1'b0));
  Seven_Seg_Hex seven_seg_hex_7 (.d(PC_OUT[3:0]), .dp(1'b0));
  Seven_Seg_Hex seven_seg_hex_8 (.d(d_ff_8_q), .dp(1'b0));
  and and_14 (and_14_out, d_ff_10_nq, CONT4);
  D_FF d_ff_10 (.D(and_14_out), .C(~MAIN_CLOCK), .Q(d_ff_10_q), .nQ(d_ff_10_nq));
  assign driverinvsel_5_out = ~PRMGR_ACT ? {PC_OUT, or_8_out[0]} : 17'bz;  // DriverInvSel driverinvsel_5
  PullDown pulldown_3 (.out(PRMGR_ACT));
  or or_5 (or_5_out, RST, decoder_1_out_4);
  or or_6 (or_6_out, decoder_1_out_0, decoder_1_out_1, CONT, decoder_1_out_3);
  Counter #(.Bits(3)) counter_1 (.en(or_6_out), .C(MAIN_CLOCK), .clr(or_5_out), .out(counter_1_out));  // open: ovf
  assign driverinvsel_5_out = PRMGR_ACT ? PRGMR_A : 17'bz;  // Driver driver_20
  PullDown pulldown_4 (.out(PRMR_WE));
  Decoder #(.Selector_Bits(3)) decoder_1 (
    .sel(counter_1_out), .out_0(decoder_1_out_0), .out_1(decoder_1_out_1), .out_2(decoder_1_out_2),
    .out_3(decoder_1_out_3), .out_4(decoder_1_out_4));  // open: out_5, out_6, out_7
  D_FF #(.Bits(4)) d_ff_11 (.D(LOW_INS_q[11:8]), .C(delay_4_out), .Q(d_ff_11_q));  // open: nQ
  and and_15 (and_15_out, SET_OVR, ~CONT6);  // And
  or or_7 (or_7_out, decoder_1_out_0, decoder_4_out_1);
  or or_8 (or_8_out[0], decoder_4_out_2, decoder_1_out_1);
  EEPROM #(.AddrBits(17), .Bits(8)) GLS29EE010_70_4C_PHE__EEPROM (
    .A(driverinvsel_5_out), .CS(1'b1), .WE(PRMR_WE), .OE(~PRMGR_ACT), .D(GLS29EE010_70_4C_PHE__EEPROM_d));
  or or_9 (or_9_out, decoder_1_out_3, RST, decoder_1_out_2);
  and and_16 (and_16_out, and_27_out, decoder_2_out_7);
  D_FF d_ff_12 (.D(and_16_out), .C(delay_4_out), .Q(CONT7));  // open: nQ
  assign GLS29EE010_70_4C_PHE__EEPROM_d = PRMGR_ACT ? PRMR_DATA : 8'bz;  // Driver driver_21
  Decoder #(.Selector_Bits(3)) decoder_2 (
    .sel(LOW_INS_q[2:0]), .out_0(decoder_2_out_0), .out_1(decoder_2_out_1), .out_2(decoder_2_out_2),
    .out_3(decoder_2_out_3), .out_4(decoder_2_out_4), .out_5(decoder_2_out_5), .out_6(decoder_2_out_6),
    .out_7(decoder_2_out_7));
  and and_17 (and_17_out, and_27_out, decoder_2_out_6);
  D_FF d_ff_13 (.D(and_17_out), .C(delay_4_out), .Q(SET_OVR));  // open: nQ
  D_FF #(.Bits(8)) HIGH_INS (.D(GLS29EE010_70_4C_PHE__EEPROM_d), .C(and_18_out), .Q(LOW_INS_q[15:8]));  // open: nQ
  and and_18 (and_18_out, MAIN_CLOCK, or_7_out);
  and and_19 (and_19_out, and_27_out, decoder_2_out_5);
  D_FF d_ff_14 (.D(and_19_out), .C(delay_4_out), .Q(CONT5));  // open: nQ
  and and_20 (and_20_out, or_9_out, ~and_15_out, MAIN_CLOCK);  // And
  D_FF #(.Bits(8)) LOW_INS (.D(GLS29EE010_70_4C_PHE__EEPROM_d), .C(and_22_out), .Q(LOW_INS_q[7:0]));  // open: nQ
  and and_21 (and_21_out, and_27_out, decoder_2_out_4);
  D_FF d_ff_15 (.D(and_21_out), .C(delay_4_out), .Q(CONT4));  // open: nQ
  Delay delay_1 (.in(and_20_out), .out(delay_1_out));
  Delay delay_2 (.in(delay_3_out), .out(delay_2_out));
  assign DATA_WRITE = SET_DIV ? LOW_INS_q : 16'bz;  // Driver driver_22
  and and_22 (and_22_out, ~MAIN_CLOCK, or_8_out[0]);  // And
  and and_23 (and_23_out, and_27_out, decoder_2_out_3);
  D_FF d_ff_16 (.D(and_23_out), .C(delay_4_out), .Q(d_ff_16_q));  // open: nQ
  Delay delay_3 (.in(delay_1_out), .out(delay_3_out));
  Delay delay_4 (.in(delay_2_out), .out(delay_4_out));
  or or_10 (or_10_out, or_12_out, decoder_1_out_3, RST);
  and and_24 (and_24_out, ~decoder_1_out_4, ~decoder_1_out_3, CONT1);  // And
  and and_25 (and_25_out, and_27_out, decoder_2_out_2);
  D_FF d_ff_17 (.D(and_25_out), .C(delay_4_out), .Q(d_ff_17_q));  // open: nQ
  and and_26 (and_26_out, and_27_out, decoder_2_out_1);
  D_FF d_ff_18 (.D(and_26_out), .C(delay_4_out), .Q(CONT1));  // open: nQ
  not not_1 (not_1_out, LOW_INS_q[3]);
  and and_27 (and_27_out, not_1_out, ~delay_6_out);  // And
  and and_28 (and_35_out[0], decoder_2_out_0, and_37_out);
  and and_29 (and_35_out[1], decoder_2_out_1, and_37_out);
  and and_30 (and_35_out[2], decoder_2_out_2, and_37_out);
  and and_31 (and_35_out[3], decoder_2_out_3, and_37_out);
  and and_32 (and_35_out[4], decoder_2_out_4, and_37_out);
  and and_33 (and_35_out[5], decoder_2_out_5, and_37_out);
  and and_34 (and_35_out[6], decoder_2_out_6, and_37_out);
  and and_35 (and_35_out[7], decoder_2_out_7, and_37_out);
  and and_36 (and_36_out, and_27_out, decoder_2_out_0);
  D_FF d_ff_19 (.D(and_36_out), .C(delay_4_out), .Q(d_ff_19_q));  // open: nQ
  LED led_1 (.in(d_ff_19_q));
  or or_11 (or_11_out, decoder_4_out_2, CONT2_WE, and_24_out, CONT_ALU);
  and and_37 (and_37_out, ~delay_6_out, LOW_INS_q[3]);  // And
  D_FF d_ff_20 (.D(and_37_out), .C(delay_4_out), .Q(d_ff_20_q));  // open: nQ
  Delay delay_5 (.in(delay_7_out), .out(delay_5_out));
  Delay delay_6 (.in(delay_5_out), .out(delay_6_out));
  Delay delay_7 (.in(delay_8_out), .out(delay_7_out));
  Delay delay_8 (.in(or_10_out), .out(delay_8_out));
  assign DATA_WRITE = CONT1 ? DATA_READ : 16'bz;  // Driver driver_23
  and and_38 (and_38_out, d_ff_20_q, ~or_12_out);  // And
  Break break_1 (.brk(CONT7));
  or or_12 (or_12_out, CONT6, decoder_4_out_2);
  or or_13 (or_13_out, RST, or_10_out, CONT_ALU);
  or or_14 (or_14_out, RST, CONT6);
  Counter #(.Bits(2)) counter_2 (.en(and_38_out), .C(MAIN_CLOCK), .clr(or_13_out), .out(counter_2_out));  // open: ovf
  or or_15 (or_15_out, d_ff_16_q, d_ff_17_q);
  Counter #(.Bits(2)) counter_3 (.en(SET_OVR), .C(MAIN_CLOCK), .clr(or_14_out), .out(counter_3_out));  // open: ovf
  or or_16 (SET_DIV, decoder_4_out_2, CONT6);
  and and_39 (and_39_out, d_ff_24_nq, d_ff_21_nq, or_15_out, ~or_10_out);  // And
  Decoder #(.Selector_Bits(2)) decoder_3 (
    .sel(counter_2_out), .out_1(ALU_IF_EN), .out_2(decoder_3_out_2), .out_3(CONT_ALU));  // open: out_0
  D_FF d_ff_21 (.D(and_39_out), .C(MAIN_CLOCK), .Q(IF_EN), .nQ(d_ff_21_nq));
  Decoder #(.Selector_Bits(2)) decoder_4 (
    .sel(counter_3_out), .out_0(decoder_4_out_0), .out_1(decoder_4_out_1), .out_2(decoder_4_out_2),
    .out_3(CONT6));
  D_FF #(.Bits(16)) d_ff_22 (.D(DATA_READ), .C(ALU_IF_EN), .Q(d_ff_22_q));  // open: nQ
  D_FF #(.Bits(16)) d_ff_23 (.D(DATA_READ), .C(decoder_3_out_2), .Q(d_ff_23_q));  // open: nQ
  and and_40 (and_40_out, SET_OVR, decoder_4_out_0);
  D_FF d_ff_24 (.D(IF_EN), .C(MAIN_CLOCK), .Q(CONT2), .nQ(d_ff_24_nq));
  or or_17 (or_17_out, DATA_READ[0], DATA_READ[1], DATA_READ[2], DATA_READ[3], DATA_READ[4], DATA_READ[5], DATA_READ[6], DATA_READ[7], DATA_READ[8], DATA_READ[9], DATA_READ[10], DATA_READ[11], DATA_READ[12], DATA_READ[13], DATA_READ[14], DATA_READ[15]);
  and and_41 (and_41_out, IF_EN, ~MAIN_CLOCK);  // And
  or or_18 (or_18_out, CONT5, CONT4);
  or or_19 (or_19_out, CONT7, CONT6);
  and and_42 (CONT2_WE, xor_1_out, CONT2);
  or or_20 (or_20_out, CONT2, or_18_out);
  or or_21 (or_21_out, or_19_out, CONT_ALU);
  assign DATA_WRITE = CONT_ALU ? driver_26_out : 16'bz;  // Driver driver_24
  D_FF d_ff_25 (.D(or_17_out), .C(and_41_out), .Q(d_ff_25_q));  // open: nQ
  or or_22 (or_22_out, CONT1, or_21_out);
  D_FF #(.Bits(8)) d_ff_26 (.D(and_35_out), .C(ALU_IF_EN), .Q(d_ff_26_q));  // open: nQ
  xor xor_1 (xor_1_out, d_ff_25_q, d_ff_16_q);
  or or_23 (CONT, or_20_out, or_22_out);
  and and_43 (and_43_out, CONT2, xor_1_out);
  and and_44 (and_44_out, d_ff_26_q[7], comparator_1_eq);
  and and_45 (and_45_out, d_ff_26_q[6], comparator_1_gt);
  assign DATA_WRITE = and_43_out ? DATA_READ : 16'bz;  // Driver driver_25
  Comparator #(.Signed("true"), .Bits(16)) comparator_1 (
    .a(d_ff_22_q), .b(d_ff_23_q), .gt(comparator_1_gt), .eq(comparator_1_eq));  // open: lt
  assign driver_26_out = or_24_out ? {16{1'b1}} : 16'bz;  // Driver driver_26
  PullDown #(.Bits(16)) pulldown_5 (.out(driver_26_out));
  assign driver_26_out = d_ff_26_q[5] ? mul_1_mul[15:0] : 16'bz;  // Driver driver_27
  or or_24 (or_24_out, and_45_out, and_44_out);
  Mul #(.Bits(16)) mul_1 (.a(d_ff_23_q), .b(d_ff_22_q), .mul(mul_1_mul));
  assign driver_26_out = d_ff_26_q[4] ? driver_35_out : 16'bz;  // Driver driver_28
  Add #(.Bits(16)) add_2 (.a(d_ff_23_q), .b(d_ff_22_q), .c_i(1'b0), .s(add_2_s));  // open: c_o
  assign not_2_out = ~d_ff_22_q;  // Not not_2, 16 bits wide
  assign driver_26_out = d_ff_26_q[3] ? add_2_s : 16'bz;  // Driver driver_29
  assign driver_26_out = d_ff_26_q[2] ? not_2_out : 16'bz;  // Driver driver_30
  and and_46 (and_46_out, ~and_53_out, or_26_out);  // And
  and and_47 (and_47_out, or_26_out, and_53_out);
  assign or_25_out = d_ff_23_q | d_ff_22_q;  // Or or_25, 16 bits wide
  assign driver_26_out = d_ff_26_q[1] ? or_25_out : 16'bz;  // Driver driver_31
  assign and_48_out = d_ff_23_q & d_ff_22_q;  // And and_48, 16 bits wide
  assign driver_26_out = d_ff_26_q[0] ? and_48_out : 16'bz;  // Driver driver_32
  assign driver_33_out = and_46_out ? driverinvsel_4_out : 16'bz;  // Driver driver_33
  assign driverinvsel_4_out = and_47_out ? driver_33_out : 16'bz;  // Driver driver_34
  assign driver_35_out = LOW_INS_q[15] ? barrelshifter_1_out : 16'bz;  // Driver driver_35
  BarrelShifter #(.Bits(16)) barrelshifter_1 (
    .in(d_ff_22_q), .shift({2'b00, LOW_INS_q[14:12]}), .out(barrelshifter_1_out));
  assign driver_35_out = ~LOW_INS_q[15] ? barrelshifter_2_out : 16'bz;  // DriverInvSel driverinvsel_6
  BarrelShifter #(.Bits(16), .direction("right")) barrelshifter_2 (
    .in(d_ff_22_q), .shift({2'b00, LOW_INS_q[14:12]}), .out(barrelshifter_2_out));
  or or_26 (or_26_out, and_53_out, d_ff_10_q);
  PullDown #(.Bits(16)) pulldown_6 (.out(driver_33_out));
  D_FF writing3 (.D(and_49_out), .C(MAIN_CLOCK), .Q(writing3_q), .nQ(writing3_nq));
  D_FF writing2 (.D(and_50_out), .C(MAIN_CLOCK), .Q(writing2_q), .nQ(writing2_nq));
  D_FF writing1 (.D(and_52_out), .C(and_51_out), .Q(writing1_q));  // open: nQ
  assign driver_36_out = d_ff_10_q ? ADDR_BUF_q : 3'bz;  // Driver driver_36
  PullDown #(.Bits(3)) pulldown_7 (.out(driver_36_out));
  and and_49 (and_49_out, writing3_nq, writing2_q);
  and and_50 (and_50_out, writing2_nq, and_71_out, writing1_q);
  and and_51 (and_51_out, MAIN_CLOCK, or_28_out);
  and and_52 (and_52_out, initial_q, ~RST, driver_42_out[0]);  // And
  or or_27 (or_27_out, d_ff_29_q, d_ff_10_q, and_70_out, TB4);
  or or_28 (or_28_out, RST, and_71_out);
  and and_53 (and_53_out, ~d_ff_10_q, or_27_out, and_59_out);  // And
  and and_54 (and_54_out, MAIN_CLOCK, and_66_out, ~writing1_q, ~writing2_q, ~writing3_q);  // And
  or or_29 (or_29_out, writing3_q, reading2_q);
  D_FF reading2 (.D(and_55_out), .C(MAIN_CLOCK), .Q(reading2_q), .nQ(reading2_nq));
  D_FF reading1 (.D(and_57_out), .C(and_56_out), .Q(reading1_q));  // open: nQ
  D_FF \initial  (.D(or_30_out), .C(and_58_out), .Q(initial_q));  // open: nQ
  D_FF #(.Bits(9)) d_ff_27 (.D(driver_42_out_2), .C(and_54_out), .Q(d_ff_27_q));  // open: nQ
  and and_55 (and_55_out, reading2_nq, reading1_q);
  and and_56 (and_56_out, or_32_out, MAIN_CLOCK);
  and and_57 (and_57_out, initial_q, ~RST, ~driver_42_out[0]);  // And
  and and_58 (and_58_out, or_33_out, MAIN_CLOCK);
  or or_30 (or_30_out, or_29_out, RST);
  and and_59 (and_59_out, ~driver_36_out[0], ~driver_36_out[1], ~driver_36_out[2]);  // And
  or or_31 (or_31_out[9], reading2_q, writing3_q);
  or or_32 (or_32_out, reading1_q, RST, and_66_out);
  or or_33 (or_33_out, or_29_out, RST, and_66_out);
  and and_60 (and_60_out, ~and_71_out, or_37_out);  // And
  and and_61 (and_61_out, or_37_out, and_71_out);
  not not_3 (not_3_out, MAIN_CLOCK);
  and and_62 (and_62_out, not_3_out, reset_1_out);
  Reset reset_1 (.out(reset_1_out));
  Counter #(.Bits(2)) counter_4 (.en(or_35_out), .C(and_62_out), .clr(1'b0), .out(counter_4_out));  // open: ovf
  or or_34 (or_34_out, writing2_q, writing3_q, writing1_q);
  assign driver_33_out = and_60_out ? driver_38_out : 16'bz;  // Driver driver_37
  or or_35 (or_35_out, and_63_out, RST);
  or or_36 (or_36_out, delay_9_out, writing3_q);
  assign driver_38_out = and_61_out ? driver_33_out : 16'bz;  // Driver driver_38
  // Probe CLK on MAIN_CLOCK
  and and_63 (and_63_out, ~counter_4_out[0], ~counter_4_out[1]);  // And
  Delay delay_9 (.in(delay_10_out), .out(delay_9_out));
  RAMSinglePortSel #(.AddrBits(10), .Bits(8)) ramsingleportsel_1 (
    .A({or_31_out[9], d_ff_27_q}), .CS(1'b1), .WE(or_36_out), .OE(~or_34_out), .D(ramsingleportsel_1_d));
  and and_64 (RST, counter_4_out[0], ~counter_4_out[1]);  // And
  Delay delay_10 (.in(delay_11_out), .out(delay_10_out));
  Delay delay_11 (.in(delay_12_out), .out(delay_11_out));
  Delay delay_12 (.in(delay_13_out), .out(delay_12_out));
  assign ramsingleportsel_1_d = writing3_q ? WRITE_BUFFER_q : 8'bz;  // Driver driver_39
  D_FF #(.Bits(8)) WRITE_BUFFER (.D(driver_45_out_2), .C(and_65_out), .Q(WRITE_BUFFER_q));  // open: nQ
  and and_65 (and_65_out, and_71_out, MAIN_CLOCK);
  and and_66 (and_66_out, ~writing1_q, and_71_out);  // And
  assign driver_36_out = and_70_out ? ADDR_BUFFER_q : 3'bz;  // Driver driver_40
  or or_37 (or_37_out, and_71_out, and_70_out);
  Delay delay_13 (.in(and_67_out), .out(delay_13_out));
  assign ramsingleportsel_1_d = writing2_q ? d_ff_28_q : 8'bz;  // Driver driver_41
  D_FF #(.Bits(8)) d_ff_28 (.D(driver_45_out), .C(and_65_out), .Q(d_ff_28_q));  // open: nQ
  and and_67 (and_67_out, and_71_out, MAIN_CLOCK);
  and and_68 (and_68_out, ~MAIN_CLOCK, reading1_q);  // And
  and and_69 (and_69_out, MAIN_CLOCK, and_66_out, ~writing3_q, ~writing2_q);  // And
  and and_70 (and_70_out, ~MAIN_CLOCK, or_29_out);  // And
  D_FF #(.Bits(3)) ADDR_BUFFER (.D(driver_42_out_3), .C(and_69_out), .Q(ADDR_BUFFER_q));  // open: nQ
  and and_71 (and_71_out, ~and_70_out, or_27_out, and_75_out);  // And
  PullDown #(.Bits(8)) pulldown_8 (.out(ramsingleportsel_1_d));
  D_FF #(.Bits(8)) READ_BUFFER (.D(ramsingleportsel_1_d), .C(and_68_out), .Q(READ_BUFFER_q));  // open: nQ
  and and_72 (and_72_out, ~and_78_out, or_39_out);  // And
  and and_73 (and_73_out, or_39_out, and_78_out);
  and and_74 (and_74_out, ~or_29_out, ~writing1_q);  // And
  or or_38 (or_38_out, writing1_q, writing2_q);
  and and_75 (and_75_out, ~xor_2_out[0], ~xor_2_out[1], ~xor_2_out[2]);  // And
  assign xor_2_out = driver_36_out ^ 3'b001;  // XOr xor_2, 3 bits wide
  assign {driver_42_out_3, driver_42_out_2, driver_42_out} = and_74_out ? driver_38_out : 16'bz;  // Driver driver_42
  and and_76 (and_76_out, or_38_out, ~or_29_out);  // And
  assign driver_33_out = and_72_out ? {driver_46_out_3, driver_46_out[7:4], driver_46_out_2, driver_46_out[0]} : 16'bz;  // Driver driver_43
  PullDown pulldown_9 (.out(driver_42_out[0]));
  assign driver_38_out = or_29_out ? {ramsingleportsel_1_d, READ_BUFFER_q} : 16'bz;  // Driver driver_44
  assign {driver_45_out_2, driver_45_out} = and_76_out ? driver_38_out : 16'bz;  // Driver driver_45
  assign {driver_46_out_3, driver_46_out[7:4], driver_46_out_2, driver_46_out[0]} = and_73_out ? driver_33_out : 16'bz;  // Driver driver_46
  Keyboard keyboard_1 (.C(d_ff_30_q), .D(keyboard_1_d));  // open: en, av
  D_FF d_ff_29 (.D(d_ff_30_q), .C(~MAIN_CLOCK), .Q(d_ff_29_q));  // open: nQ
  assign {driver_46_out_3, driver_46_out[7:4], driver_46_out_2, driver_46_out[0]} = d_ff_29_q ? keyboard_1_d : 16'bz;  // Driver driver_47
  D_FF d_ff_30 (.D(and_77_out), .C(MAIN_CLOCK), .Q(d_ff_30_q));  // open: nQ
  or or_39 (or_39_out, and_78_out, d_ff_29_q);
  and and_77 (and_77_out, ~RST, driver_46_out[0]);  // And
  assign driver_36_out = d_ff_29_q ? d_ff_31_q : 3'bz;  // Driver driver_48
  Terminal #(.termWidth(80)) terminal_1 (.D(driver_46_out_3), .C(and_79_out));  // open: en
  D_FF #(.Bits(3)) d_ff_31 (.D(driver_46_out_2), .C(and_77_out), .Q(d_ff_31_q));  // open: nQ
  and and_78 (and_78_out, ~d_ff_29_q, or_27_out, and_80_out);  // And
  and and_79 (and_79_out, ~driver_46_out[0], and_78_out, MAIN_CLOCK);  // And
  and and_80 (and_80_out, ~xor_3_out[0], ~xor_3_out[1], ~xor_3_out[2]);  // And
  assign xor_3_out = driver_36_out ^ 3'b010;  // XOr xor_3, 3 bits wide
  and and_81 (and_81_out, ~FB4, or_40_out);  // And
  and and_82 (and_82_out, or_40_out, FB4);
  assign driver_33_out = and_81_out ? D4 : 16'bz;  // Driver driver_49
  assign D4 = and_82_out ? driver_33_out : 16'bz;  // Driver driver_50
  assign driver_36_out = TB4 ? A4 : 3'bz;  // Driver driver_51
  or or_40 (or_40_out, FB4, TB4);
  and and_83 (FB4, ~TB4, or_27_out, and_84_out);  // And
  and and_84 (and_84_out, ~xor_4_out[0], ~xor_4_out[1], ~xor_4_out[2]);  // And
  assign xor_4_out = driver_36_out ^ 3'b011;  // XOr xor_4, 3 bits wide

  // Other names for the same wires on the sheet: CLK = MAIN_CLOCK

  // Notes on the sheet:
  //   MAIN_CLOCK: Hz: 500
  //   Program
  //   Counter:
  //   DBG
  //   Register H:
  //   NOTE: REG_ADDR_WRITE is second parameter,
  //   therefore it can be abused as literal for BUS addr.
  //   TB
  //   ADDR
  //   DATA
  //   FB
  //   0: INS_LOAD_LOW
  //   1: INS_LOAD_HIGH
  //   2: WAITING_FOR_INS_EXEC
  //   3: CLEANUP
  //   4: PC_INCREMENT
  //   contents of GLS29EE010_70_4C_PHE__EEPROM (hex, n*v repeats v):
  //   a,6,1,ff,6,6,0,8,3,6,ff,0,2,6,0,10,7,21,9,6,65,48,c8,7c,d8,89,1,84,1,94,d7,7b,9,6,
  //   6c,6c,c8,7c,d8,89,1,84,1,94,d7,7b,9,6,2c,6f,c8,7c,d8,89,1,84,1,94,d7,7b,9,6,77,20,
  //   c8,7c,d8,89,1,84,1,94,d7,7b,9,6,72,6f,c8,7c,d8,89,1,84,1,94,d7,7b,9,6,64,6c,c8,7c,
  //   d8,89,1,84,1,94,d7,7b,9,6,a,21,c8,7c,d8,89,1,84,1,94,d7,7b,7,21,4,6,0,17,ea,ab,9,
  //   6,0,54,c8,ac,d8,89,1,84,1,b4,0,7,b,91,da,ab,d7,7b,9,6,0,51,48,7f,8b,93,7,21,d1,1b,
  //   9,6,0,62,68,1f,8b,92,8,6,0,3c,b,81,c8,7c,1,84,0,f1,c5,c,c5,5c,2,54,35,8,2,54,c8,ac,
  //   1,84,8,f1,d8,8b,d8,8b,b,81
  //   ALU BIT
  //   HALTED
  //   MOVNZ
  //   MOVEZ
  //   STATE REGISTERS
  //   TB
  //   HIGH-ADDR
  //   FB cutoff
  //   on write
  //   IDT6116 allows write during WE,
  //   not just on rising edge
  //   Delay not needed IRL
endmodule
