// Digital circuit Reset On First Clock.dig as structural Verilog
module Reset_On_First_Clock (
  input  CLK,
  output RST
);

  wire and_1_out, and_2_out, not_1_out, or_1_out, reset_1_out;
  wire [1:0] counter_1_out;

  not not_1 (not_1_out, CLK);
  and and_1 (and_1_out, not_1_out, reset_1_out);
  Reset reset_1 (.out(reset_1_out));
  Counter #(.Bits(2)) counter_1 (.en(or_1_out), .C(and_1_out), .clr(1'b0), .out(counter_1_out));  // open: ovf
  or or_1 (or_1_out, and_2_out, RST);
  and and_2 (and_2_out, ~counter_1_out[0], ~counter_1_out[1]);  // And
  and and_3 (RST, counter_1_out[0], ~counter_1_out[1]);  // And
endmodule
